// Digital circuit Exam 1-1 Template.dig as structural Verilog
module Exam_1_1_Template (
  input  X1,
  input  X2,
  input  X3,
  input  X4,
  output Y1,
  output [4:0] CheckGlitch
);

  wire and_1_out, and_2_out, not_1_out;

  not not_1 (not_1_out, X3);
  and and_1 (and_1_out, X2, X3, X4);
  and and_2 (and_2_out, X1, not_1_out);
  or or_1 (Y1, and_1_out, and_2_out);
  Counter #(.Bits(5)) counter_1 (.en(1'b1), .C(Y1), .clr(1'b0), .out(CheckGlitch));  // open: ovf

  // Notes on the sheet:
  //   Must not change this section
endmodule

/* Test case:
X1 X2 X3 X4 Y1
0 0 0 0 0
0 0 0 1 0
0 0 1 0 0
0 0 1 1 0
0 1 0 0 0
0 1 0 1 0
0 1 1 0 0
0 1 1 1 1
1 0 0 0 1
1 0 0 1 1
1 0 1 0 0
1 0 1 1 0
1 1 0 0 1
1 1 0 1 1
1 1 1 0 0
1 1 1 1 1
*/
