// Digital circuit test.dig as structural Verilog
module test (
  input  X1,
  input  X2,
  input  X3,
  input  X4,
  output Y1,
  output [4:0] CheckGlitch
);

  wire not_1_out, not_2_out, not_3_out, not_4_out, or_1_out, or_2_out, or_3_out;

  not not_1 (not_1_out, X1);
  not not_2 (not_2_out, X2);
  not not_3 (not_3_out, X3);
  not not_4 (not_4_out, X4);
  or or_1 (or_1_out, X1, X3);
  or or_2 (or_2_out, X2, not_3_out);
  or or_3 (or_3_out, not_3_out, X4);
  and and_1 (Y1, or_1_out, or_2_out, or_3_out);
  Counter #(.Bits(5)) counter_1 (.en(1'b1), .C(Y1), .clr(1'b0), .out(CheckGlitch));  // open: ovf

  // Notes on the sheet:
  //   Must not change this section
endmodule

/* Test case:
X1 X2 X3 X4 Y1
0 0 0 0 0
0 0 0 1 0
0 0 1 0 0
0 0 1 1 0
0 1 0 0 0
0 1 0 1 0
0 1 1 0 0
0 1 1 1 1
1 0 0 0 1
1 0 0 1 1
1 0 1 0 0
1 0 1 1 0
1 1 0 0 1
1 1 0 1 1
1 1 1 0 0
1 1 1 1 1
*/
