// Digital circuit Exam 1-2 Template.dig as structural Verilog
module Exam_1_2_Template (
  input  X1,
  input  X0,
  input  Y1,
  input  Y0,
  output [4:0] Z
);

  wire and_1_out, and_2_out, and_3_out, and_4_out, and_5_out, not_1_out, not_2_out, not_3_out, not_4_out;

  not not_1 (not_1_out, X1);
  not not_2 (not_2_out, X0);
  not not_3 (not_3_out, Y1);
  not not_4 (not_4_out, Y0);
  and and_1 (and_1_out, X1, Y1, Y0);
  and and_2 (and_2_out, X1, X0, Y1);
  and and_3 (and_3_out, X1, X0, Y1, Y0);
  and and_4 (and_4_out, X1, not_3_out, Y0);
  and and_5 (and_5_out, not_3_out, not_4_out);
  and and_6 (Z[4], X1, X0, Y1, Y0);
  or or_1 (Z[3], and_1_out, and_2_out);
  and and_7 (Z[2], X1, not_2_out, Y1, not_4_out);
  or or_2 (Z[1], and_3_out, and_4_out);
  or or_3 (Z[0], and_5_out, X0);
endmodule

/* Test case:
X1 X0 Y1 Y0 Z
0 0 0 0 0b00001
0 0 0 1 0b00000
0 0 1 0 0b00000
0 0 1 1 0b00000
0 1 0 0 0b00001
0 1 0 1 0b00001
0 1 1 0 0b00001
0 1 1 1 0b00001
1 0 0 0 0b00001
1 0 0 1 0b00010
1 0 1 0 0b00100
1 0 1 1 0b01000
1 1 0 0 0b00001
1 1 0 1 0b00011
1 1 1 0 0b01001
1 1 1 1 0b11011
*/
