// Digital circuit Exam 1-3 Template.dig as structural Verilog
module Exam_1_3_Template (
  input  A1,
  input  A2,
  input  A3,
  input  B1,
  input  B2,
  input  B3,
  input  B4,
  output Y
);

  wire and_1_out, and_2_out, and_3_out, and_4_out, and_5_out, and_6_out, and_7_out, and_8_out, and_9_out,
       or_1_out, or_2_out;

  and and_1 (and_1_out, A1, A2);
  and and_2 (and_2_out, A1, A3);
  and and_3 (and_3_out, A2, A3);
  and and_4 (and_4_out, B1, B4);
  and and_5 (and_5_out, B1, B3);
  and and_6 (and_6_out, B1, B2);
  and and_7 (and_7_out, B2, B4);
  and and_8 (and_8_out, B2, B3);
  and and_9 (and_9_out, B3, B4);
  or or_1 (or_1_out, and_1_out, and_2_out, and_3_out);
  or or_2 (or_2_out, and_4_out, and_5_out, and_6_out, and_7_out, and_8_out, and_9_out);
  or or_3 (Y, or_1_out, or_2_out);
endmodule
