// Digital circuit Template_04.dig as structural Verilog
module Template_04 (
  input  [7:0] M,
  input  [7:0] N,
  input  [12:0] progIN,
  input  reset,
  input  progLoad,
  input  start,
  input  result,
  input  clk,
  output valid,
  output done,
  output [7:0] \output ,
  output [7:0] cnt,
  output [7:0] r_cnt,
  output [12:0] out_14,
  output [7:0] out_15,
  output [7:0] out_16,
  output [7:0] out_17,
  output [7:0] out_18,
  output [7:0] out_19,
  output [7:0] out_20
);

  wire _00, _00000, _00001, _01, _00010, _10, _00011, _11, _00100, _00101, _00110, _00111, _01000, _01001,
       _01010, _01011, _01100, _01101, _01110, _01111, _10000, _10001, _10010, _10011, _10100, _10101,
       _10110, _10111, _11000, _11001, _11010, _11011, _11100, _11101, _11110, _11111, _11111op, and_1_out,
       and_2_out, and_4_out, and_5_out, and_6_out, and_7_out, and_8_out, and_9_out, and_10_out, and_11_out,
       and_12_out, and_13_out, and_14_out, and_15_out, and_16_out, and_17_out, and_18_out, and_19_out,
       and_20_out, and_21_out, and_22_out, and_23_out, and_24_out, and_25_out, and_26_out, and_27_out,
       and_28_out, and_29_out, d_ff_1_nq, d_ff_2_q, d_ff_3_q, en_rRAM, enA, enB, enC, eq, eq_t, gr, gt,
       isprimefinal_1_p2, le, lt, multiplexer_5_out, multiplexer_11_out, multiplexer_13_out,
       multiplexer_14_out, multiplexer_15_out, multiplexer_16_out, multiplexer_17_out, multiplexer_18_out,
       multiplexer_19_out, not_1_out, not_2_out, not_3_out, not_4_out, not_5_out, not_6_out, not_7_out,
       or_1_out, or_2_out, or_3_out, or_4_out, or_7_out, or_8_out, or_9_out, or_10_out, or_16_out, or_17_out,
       P_a, P_b, Q_a, Q_a_plus__op, Q_b, Q_b_plus__op, Q_c, Q_c_plus__op, Q_d, Q_d_plus__op, Q_e,
       Q_e_plus__op, r_cnt_eq_16, r_cnt_eq_cnt, r_cnt_gt_16, r_cnt_gt_cnt, r_cnt_lt_16, r_cnt_lt_cnt,
       result_cnt_eq_16, result_cnt_gt_16, result_cnt_lt_16, start_t;
  wire [4:0] opcode;
  wire [7:0] multiplexer_1_out, multiplexer_4_out, multiplexer_6_out, multiplexer_7_out, multiplexer_8_out,
       multiplexer_9_out, multiplexer_10_out, multiplexer_12_out, operand, pRAM_operand, rRAM_operand,
       undriven, val;
  wire [12:0] multiplexer_2_out, multiplexer_3_out;
  wire [12:8] pRAM_reserve_d2;

  or or_1 (or_1_out, _00010, _00100);
  not not_1 (not_1_out, _00010);
  or or_2 (or_2_out, _00000, _11100);
  and and_1 (and_1_out, not_1_out, _00011);
  Multiplexer #(.Bits(8)) multiplexer_1 (.sel(_11011), .in_0({8{1'b0}}), .in_1(operand), .out(multiplexer_1_out));
  Counter #(.Bits(8)) result_cnt (.en(_01), .C(clk), .clr(_00), .out(out_19));  // open: ovf
  Comparator #(.Bits(8)) comparator_1 (
    .a(out_19), .b(8'h10), .gt(result_cnt_gt_16), .eq(result_cnt_eq_16), .lt(result_cnt_lt_16));
  CounterPreset #(.maxValue(256), .Bits(8)) u_cnt (
    .en(progLoad), .C(clk), .dir(1'b0), .in({8{1'b0}}), .ld(1'b0), .clr(and_1_out), .out(cnt));  // open: ovf
  CounterPreset #(.maxValue(256), .Bits(8)) u_r_cnt (
    .en(or_1_out), .C(clk), .dir(1'b0), .in({8{1'b0}}), .ld(1'b0), .clr(or_2_out), .out(r_cnt));  // open: ovf
  Comparator #(.Bits(8)) u_r_cnt_eq_16 (.a(r_cnt), .b(8'h10), .gt(r_cnt_gt_16), .eq(r_cnt_eq_16), .lt(r_cnt_lt_16));
  Comparator #(.Bits(8)) u_r_cnt_eq_cnt (.a(r_cnt), .b(cnt), .gt(r_cnt_gt_cnt), .eq(r_cnt_eq_cnt), .lt(r_cnt_lt_cnt));
  CounterPreset #(.maxValue(256), .Bits(8)) pc (
    .en(_11010), .C(clk), .dir(1'b0), .in(multiplexer_1_out), .ld(_11011), .clr(_00000), .out(out_20));  // open: ovf
  D_FF d_ff_1 (.D(start), .C(clk), .nQ(d_ff_1_nq));  // open: Q
  Multiplexer #(.Bits(13)) multiplexer_2 (.sel(_00010), .in_0(progIN), .in_1({13{1'b0}}), .out(multiplexer_2_out));
  Multiplexer #(.Bits(13)) multiplexer_3 (.sel(_00010), .in_0(progIN), .in_1({13{1'b0}}), .out(multiplexer_3_out));
  Multiplexer #(.Bits(8)) multiplexer_4 (.sel(_00100), .in_0(operand), .in_1(r_cnt), .out(multiplexer_4_out));
  Multiplexer multiplexer_5 (.sel(_00011), .in_0(_11100), .in_1(1'b0), .out(multiplexer_5_out));
  and and_2 (and_2_out, _10, ~_00100);  // And
  or or_3 (or_3_out, progLoad, _00010);
  Multiplexer #(.Bits(8)) multiplexer_6 (.sel(_00010), .in_0(cnt), .in_1(r_cnt), .out(multiplexer_6_out));
  Multiplexer #(.Bits(8)) multiplexer_7 (.sel(en_rRAM), .in_0(r_cnt), .in_1(operand), .out(multiplexer_7_out));
  or or_4 (or_4_out, progLoad, _00010);
  Multiplexer #(.Bits(8)) multiplexer_8 (.sel(_00100), .in_0(val), .in_1({8{1'b0}}), .out(multiplexer_8_out));
  D_FF d_ff_2 (.D(start), .C(clk), .Q(d_ff_2_q));  // open: nQ
  D_FF d_ff_3 (.D(d_ff_1_nq), .C(clk), .Q(d_ff_3_q));  // open: nQ
  or or_5 (valid, multiplexer_5_out, _11111op);
  or or_6 (done, and_2_out, result_cnt_eq_16);
  Multiplexer #(.Bits(8)) multiplexer_9 (.sel(_00010), .in_0(cnt), .in_1(r_cnt), .out(multiplexer_9_out));
  or or_7 (or_7_out, en_rRAM, _00100);
  and and_3 (start_t, d_ff_2_q, d_ff_3_q);
  RAMDualAccess #(.AddrBits(8), .Bits(13)) pRAM (
    .str(or_3_out), .C(clk), .ld(1'b0), .A1(multiplexer_6_out), .Din1(multiplexer_2_out), .A2(out_20),
    .D2(out_14));  // open: D1
  or or_8 (or_8_out, en_rRAM, _00100);
  Multiplexer #(.Bits(8)) multiplexer_10 (.sel(en_rRAM), .in_0({8{1'b0}}), .in_1(val), .out(multiplexer_10_out));
  RAMDualAccess #(.AddrBits(8), .Bits(13)) pRAM_reserve (
    .str(or_4_out), .C(clk), .ld(1'b0), .A1(multiplexer_9_out), .Din1(multiplexer_3_out), .A2(operand),
    .D2({pRAM_reserve_d2, pRAM_operand}));  // open: D1
  RAMDualAccess #(.AddrBits(8), .Bits(8)) rRAM_reserve (
    .str(or_7_out), .C(clk), .ld(1'b0), .A1(multiplexer_4_out), .Din1(multiplexer_8_out), .A2(operand),
    .D2(rRAM_operand));  // open: D1
  RAMDualAccess #(.AddrBits(8), .Bits(8)) rRAM (
    .str(or_8_out), .C(clk), .ld(1'b0), .A1(multiplexer_7_out), .Din1(multiplexer_10_out), .A2(out_19),
    .D2(\output ));  // open: D1
  and and_4 (and_4_out, _00101, clk);
  D_FF #(.Bits(8)) d_ff_4 (.D(out_14[7:0]), .C(and_4_out), .Q(operand));  // open: nQ
  D_FF #(.Bits(5)) d_ff_5 (.D(out_14[12:8]), .C(and_5_out), .Q(opcode));  // open: nQ
  and and_5 (and_5_out, _00101, clk);
  Seven_Seg_Hex seven_seg_hex_1 (.d(\output [7:4]), .dp(1'b0));
  Seven_Seg_Hex seven_seg_hex_2 (.d(\output [3:0]), .dp(1'b0));
  Comparator #(.Bits(8)) comparator_2 (.a(out_15), .b(out_16), .gt(gt), .eq(eq), .lt(lt));
  // isprimeFinal isprimefinal_1: pin names not known; wires that end beside it: out_15, isprimefinal_1_p2
  Multiplexer multiplexer_11 (.sel(_11000), .in_0(eq), .in_1(isprimefinal_1_p2), .out(multiplexer_11_out));
  or or_9 (or_9_out, enA, _11001);
  or or_10 (or_10_out, _10110, _11000);
  Multiplexer #(.Bits(8)) multiplexer_12 (.sel(opcode[4]), .in_0(val), .in_1(out_18), .out(multiplexer_12_out));
  Register register_1 (.D(gt), .C(clk), .en(_10110), .Q(gr));
  Register register_2 (.D(multiplexer_11_out), .C(clk), .en(or_10_out), .Q(eq_t));
  Register register_3 (.D(lt), .C(clk), .en(_10110), .Q(le));
  Register #(.Bits(8)) accA (.D(multiplexer_12_out), .C(clk), .en(or_9_out), .Q(out_15));
  Register #(.Bits(8)) accB (.D(val), .C(clk), .en(enB), .Q(out_16));
  Register #(.Bits(8)) regC (.D(val), .C(clk), .en(enC), .Q(out_17));
  // move move_1: pin names not known; wires that end beside it: out_15, out_16, out_17, operand, pRAM_operand, rRAM_operand, M, N, opcode, enA, enB, enC, en_rRAM, val
  ALU alu_1 (.A(out_15), .B(out_16), .op(opcode[3:0]));  // open: ans
  D_FF #(.Bits(8)) d_ff_6 (.D(undriven), .C(clk), .Q(out_18));  // open: nQ
  not not_2 (not_2_out, reset);
  not not_3 (not_3_out, reset);
  not not_4 (not_4_out, result_cnt_eq_16);
  Multiplexer #(.Selector_Bits(5)) multiplexer_13 (
    .sel({Q_a, Q_b, Q_c, Q_d, Q_e}), .in_0(1'b0), .in_1(1'b0), .in_2(1'b0), .in_3(1'b0), .in_4(1'b0),
    .in_5(Q_a_plus__op), .in_6(1'b1), .in_7(1'b0), .in_8(1'b0), .in_9(1'b0), .in_10(1'b0), .in_11(1'b0),
    .in_12(1'b0), .in_13(1'b0), .in_14(1'b0), .in_15(1'b0), .in_16(1'b0), .in_17(1'b1), .in_18(1'b1),
    .in_19(1'b1), .in_20(1'b1), .in_21(1'b1), .in_22(1'b1), .in_23(1'b1), .in_24(1'b1), .in_25(1'b1),
    .in_26(1'b0), .in_27(1'b0), .in_28(not_2_out), .in_29(1'b0), .in_30(1'b0), .in_31(1'b0),
    .out(multiplexer_13_out));
  Multiplexer #(.Selector_Bits(2)) multiplexer_14 (
    .sel({P_a, P_b}), .in_0(1'b0), .in_1(result_cnt_eq_16), .in_2(not_3_out), .in_3(1'b0),
    .out(multiplexer_14_out));
  Multiplexer #(.Selector_Bits(2)) multiplexer_15 (
    .sel({P_a, P_b}), .in_0(result), .in_1(not_4_out), .in_2(1'b0), .in_3(1'b0), .out(multiplexer_15_out));
  D_FF d_ff_7 (.D(multiplexer_13_out), .C(clk), .Q(Q_a));  // open: nQ
  D_FF d_ff_8 (.D(multiplexer_14_out), .C(clk), .Q(P_a));  // open: nQ
  D_FF d_ff_9 (.D(multiplexer_15_out), .C(clk), .Q(P_b));  // open: nQ
  not not_5 (not_5_out, reset);
  Multiplexer #(.Selector_Bits(5)) multiplexer_16 (
    .sel({Q_a, Q_b, Q_c, Q_d, Q_e}), .in_0(1'b0), .in_1(1'b0), .in_2(1'b0), .in_3(1'b0), .in_4(1'b0),
    .in_5(Q_b_plus__op), .in_6(1'b1), .in_7(1'b0), .in_8(1'b0), .in_9(1'b0), .in_10(1'b0), .in_11(1'b0),
    .in_12(1'b0), .in_13(1'b0), .in_14(1'b0), .in_15(1'b0), .in_16(1'b0), .in_17(1'b1), .in_18(1'b1),
    .in_19(1'b1), .in_20(1'b1), .in_21(1'b1), .in_22(1'b1), .in_23(1'b1), .in_24(1'b1), .in_25(1'b1),
    .in_26(1'b0), .in_27(1'b0), .in_28(not_5_out), .in_29(1'b0), .in_30(1'b0), .in_31(1'b0),
    .out(multiplexer_16_out));
  Decoder #(.Selector_Bits(2)) decoder_1 (.sel({P_a, P_b}), .out_0(_00), .out_1(_01), .out_2(_10), .out_3(_11));
  and and_6 (and_6_out, ~opcode[4], ~opcode[3], ~opcode[2], ~opcode[1], ~opcode[0]);  // And
  and and_7 (and_7_out, opcode[4], opcode[3], opcode[0]);
  and and_8 (and_8_out, opcode[4], ~opcode[2], opcode[0]);  // And
  and and_9 (and_9_out, opcode[4], ~opcode[3], opcode[1], ~opcode[0]);  // And
  and and_10 (and_10_out, opcode[4], opcode[2], ~opcode[1]);  // And
  and and_11 (and_11_out, opcode[4], opcode[3], ~opcode[2]);  // And
  and and_12 (and_12_out, ~opcode[4], ~opcode[3], opcode[2]);  // And
  and and_13 (and_13_out, ~opcode[4], ~opcode[2], opcode[3]);  // And
  and and_14 (and_14_out, opcode[4], ~opcode[3], ~opcode[2], ~opcode[1], ~opcode[0]);  // And
  and and_15 (and_15_out, opcode[2], opcode[1], opcode[0]);
  and and_16 (and_16_out, opcode[4], opcode[3], opcode[2], opcode[1]);
  and and_17 (and_17_out, ~opcode[4], ~opcode[3], opcode[0]);  // And
  and and_18 (and_18_out, ~opcode[4], ~opcode[3], opcode[1]);  // And
  and and_19 (and_19_out, ~opcode[4], ~opcode[3]);  // And
  and and_20 (and_20_out, ~opcode[4], ~opcode[2]);  // And
  and and_21 (and_21_out, ~opcode[4], ~opcode[1], opcode[0]);  // And
  and and_22 (and_22_out, ~opcode[3], opcode[2], opcode[1], opcode[0]);  // And
  and and_23 (and_23_out, opcode[3], opcode[2], opcode[1], ~opcode[0]);  // And
  and and_24 (and_24_out, opcode[3], opcode[2], ~opcode[0]);  // And
  and and_25 (and_25_out, opcode[4], ~opcode[2]);  // And
  and and_26 (and_26_out, opcode[4], ~opcode[3], ~opcode[0]);  // And
  and and_27 (and_27_out, opcode[4], ~opcode[0]);  // And
  D_FF d_ff_10 (.D(multiplexer_16_out), .C(clk), .Q(Q_b));  // open: nQ
  and and_28 (and_28_out, ~opcode[3], ~opcode[2], ~opcode[1], ~opcode[0]);  // And
  and and_29 (and_29_out, opcode[3], opcode[2]);
  not not_6 (not_6_out, r_cnt_eq_16);
  not not_7 (not_7_out, reset);
  or or_11 (Q_a_plus__op, and_28_out, and_29_out, opcode[4]);
  or or_12 (Q_b_plus__op, and_6_out, and_7_out, and_8_out, and_9_out, and_10_out, and_11_out);
  or or_13 (Q_c_plus__op, and_12_out, and_13_out, and_14_out, and_15_out, and_16_out, and_17_out, and_18_out);
  or or_14 (Q_d_plus__op, and_19_out, and_20_out, and_21_out, and_22_out, and_23_out);
  or or_15 (Q_e_plus__op, and_24_out, and_25_out, and_26_out, and_27_out);
  Multiplexer #(.Selector_Bits(5)) multiplexer_17 (
    .sel({Q_a, Q_b, Q_c, Q_d, Q_e}), .in_0(start_t), .in_1(1'b0), .in_2(1'b0), .in_3(1'b1), .in_4(not_6_out),
    .in_5(Q_c_plus__op), .in_6(1'b0), .in_7(1'b0), .in_8(1'b0), .in_9(1'b0), .in_10(1'b0), .in_11(1'b0),
    .in_12(1'b0), .in_13(1'b0), .in_14(1'b0), .in_15(1'b0), .in_16(1'b0), .in_17(1'b0), .in_18(1'b0),
    .in_19(1'b0), .in_20(1'b0), .in_21(1'b0), .in_22(1'b0), .in_23(1'b0), .in_24(1'b0), .in_25(1'b0),
    .in_26(1'b1), .in_27(1'b1), .in_28(not_7_out), .in_29(1'b0), .in_30(1'b0), .in_31(1'b0),
    .out(multiplexer_17_out));
  D_FF d_ff_11 (.D(multiplexer_17_out), .C(clk), .Q(Q_c));  // open: nQ
  Multiplexer #(.Selector_Bits(5)) multiplexer_18 (
    .sel({Q_a, Q_b, Q_c, Q_d, Q_e}), .in_0(reset), .in_1(1'b0), .in_2(1'b1), .in_3(1'b0), .in_4(1'b0),
    .in_5(Q_d_plus__op), .in_6(1'b1), .in_7(1'b0), .in_8(1'b0), .in_9(1'b0), .in_10(1'b0), .in_11(1'b0),
    .in_12(1'b0), .in_13(1'b0), .in_14(1'b0), .in_15(1'b0), .in_16(1'b0), .in_17(1'b1), .in_18(1'b1),
    .in_19(1'b1), .in_20(1'b1), .in_21(1'b1), .in_22(1'b1), .in_23(1'b1), .in_24(1'b1), .in_25(1'b1),
    .in_26(1'b0), .in_27(1'b0), .in_28(reset), .in_29(1'b0), .in_30(1'b0), .in_31(1'b0),
    .out(multiplexer_18_out));
  D_FF d_ff_12 (.D(multiplexer_18_out), .C(clk), .Q(Q_d));  // open: nQ
  or or_16 (or_16_out, start_t, progLoad);
  or or_17 (or_17_out, eq_t, gr);
  Multiplexer #(.Selector_Bits(5)) multiplexer_19 (
    .sel({Q_a, Q_b, Q_c, Q_d, Q_e}), .in_0(or_16_out), .in_1(progLoad), .in_2(r_cnt_eq_cnt), .in_3(1'b0),
    .in_4(1'b0), .in_5(Q_e_plus__op), .in_6(1'b0), .in_7(1'b0), .in_8(1'b0), .in_9(1'b0), .in_10(1'b0),
    .in_11(1'b0), .in_12(1'b0), .in_13(1'b0), .in_14(1'b0), .in_15(1'b0), .in_16(1'b0), .in_17(1'b1),
    .in_18(eq_t), .in_19(gr), .in_20(le), .in_21(or_17_out), .in_22(1'b0), .in_23(1'b0), .in_24(1'b0),
    .in_25(1'b0), .in_26(1'b1), .in_27(1'b1), .in_28(1'b0), .in_29(1'b0), .in_30(1'b0), .in_31(1'b0),
    .out(multiplexer_19_out));
  D_FF d_ff_13 (.D(multiplexer_19_out), .C(clk), .Q(Q_e));  // open: nQ
  Decoder #(.Selector_Bits(5)) decoder_2 (
    .sel({Q_a, Q_b, Q_c, Q_d, Q_e}), .out_0(_00000), .out_1(_00001), .out_2(_00010), .out_3(_00011),
    .out_4(_00100), .out_5(_00101), .out_6(_00110), .out_7(_00111), .out_8(_01000), .out_9(_01001),
    .out_10(_01010), .out_11(_01011), .out_12(_01100), .out_13(_01101), .out_14(_01110), .out_15(_01111),
    .out_16(_10000), .out_17(_10001), .out_18(_10010), .out_19(_10011), .out_20(_10100), .out_21(_10101),
    .out_22(_10110), .out_23(_10111), .out_24(_11000), .out_25(_11001), .out_26(_11010), .out_27(_11011),
    .out_28(_11100), .out_29(_11101), .out_30(_11110), .out_31(_11111));
  Decoder #(.Selector_Bits(5)) decoder_3 (
    .sel(opcode), .out_31(_11111op));  // open: out_0, out_1, out_2, out_3, out_4, out_5, out_6, out_7, out_8, out_9, out_10, out_11, out_12, out_13, out_14, out_15, out_16, out_17, out_18, out_19, out_20, out_21, out_22, out_23, out_24, out_25, out_26, out_27, out_28, out_29, out_30

  // Other names for the same wires on the sheet: accA[7:0] = out_15; accB[7:0] = out_16; ALU_result[7:0] = out_18;
  //   operand__gt_pc[7:0] = operand; pc[7:0] = out_20; regC[7:0] = out_17; result_cnt[7:0] = out_19
endmodule

/* Test case 01_P01T01:
M N progIN reset progLoad start result clk valid done output	
0 0 0 0 0 0 0 0 x x x	
0 0 0 0 0 0 0 1 x x x	
0 0 0 1 0 0 0 0 x x x	
0 0 0 1 0 0 0 1 0 0 0	
0 0 0 0 0 0 0 0 0 0 0	
0 0 0 0 0 0 0 1 0 0 0	
0 0 0 0 0 0 0 0 0 0 0	
0 0 0 0 0 0 0 1 0 0 0	
0 0 0 0 0 0 0 0 0 0 0	
0 0 0 0 0 0 0 1 0 0 0	
0 0 0 0 0 0 0 0 0 0 0	
0 0 0 0 0 0 0 1 0 0 0	
0 0 0 0 0 0 0 0 0 0 0	
0 0 0 0 0 0 0 1 0 0 0	
0 0 0 0 0 0 0 0 0 0 0	
0 0 0 0 0 0 0 1 0 0 0	
0 0 0 0 0 0 0 0 0 0 0	
0 0 0 0 0 0 0 1 0 0 0	
0 0 0 0 0 0 0 0 0 0 0	
0 0 0 0 0 0 0 1 0 0 0	
0 0 0 0 0 0 0 0 0 0 0	
0 0 0 0 0 0 0 1 0 0 0	
0 0 0 0 0 0 0 0 0 0 0	
0 0 0 0 0 0 0 1 0 0 0	
0 0 0 0 0 0 0 0 0 0 0	
0 0 0 0 0 0 0 1 0 0 0	
0 0 0 0 0 0 0 0 0 0 0	
0 0 0 0 0 0 0 1 0 0 0	
0 0 0 0 0 0 0 0 0 0 0	
0 0 0 0 0 0 0 1 0 0 0	
0 0 0 0 0 0 0 0 0 0 0	
0 0 0 0 0 0 0 1 0 0 0	
0 0 0 0 0 0 0 0 0 0 0	
0 0 0 0 0 0 0 1 0 0 0	
0 0 0 0 0 0 0 0 0 0 0	
0 0 0 0 0 0 0 1 0 0 0	
0 0 0 0 0 0 0 0 0 0 0	
0 0 0 0 0 0 0 1 0 0 0	
0 0 0 0 0 0 0 0 0 0 0	
0 0 0 0 0 0 0 1 0 0 0	
0 0 0 0 0 0 0 0 0 0 0	
0 0 0 0 0 0 0 1 0 0 0	
0 0 271 0 1 0 0 0 0 0 0	
0 0 271 0 1 0 0 1 0 0 0	
0 0 566 0 1 0 0 0 0 0 0	
0 0 566 0 1 0 0 1 0 0 0	
0 0 5888 0 1 0 0 0 0 0 0	
0 0 5888 0 1 0 0 1 0 0 0	
0 0 3599 0 1 0 0 0 0 0 0	
0 0 3599 0 1 0 0 1 0 0 0	
0 0 4110 0 1 0 0 0 0 0 0	
0 0 4110 0 1 0 0 1 0 0 0	
0 0 3856 0 1 0 0 0 0 0 0	
0 0 3856 0 1 0 0 1 0 0 0	
0 0 0 0 1 0 0 0 0 0 0	
0 0 0 0 1 0 0 1 0 0 0	
0 0 0 0 1 0 0 0 0 0 0	
0 0 0 0 1 0 0 1 0 0 0	
0 0 0 0 1 0 0 0 0 0 0	
0 0 0 0 1 0 0 1 0 0 0	
0 0 0 0 1 0 0 0 0 0 0	
0 0 0 0 1 0 0 1 0 0 0	
0 0 0 0 1 0 0 0 0 0 0	
0 0 0 0 1 0 0 1 0 0 0	
0 0 0 0 1 0 0 0 0 0 0	
0 0 0 0 1 0 0 1 0 0 0	
0 0 0 0 1 0 0 0 0 0 0	
0 0 0 0 1 0 0 1 0 0 0	
0 0 0 0 1 0 0 0 0 0 0	
0 0 0 0 1 0 0 1 0 0 0	
0 0 0 0 1 0 0 0 0 0 0	
0 0 0 0 1 0 0 1 0 0 0	
0 0 0 0 1 0 0 0 0 0 0	
0 0 0 0 1 0 0 1 0 0 0	
0 0 4352 0 1 0 0 0 0 0 0	
0 0 4352 0 1 0 0 1 0 0 0	
0 0 2819 0 1 0 0 0 0 0 0	
0 0 2819 0 1 0 0 1 0 0 0	
0 0 7936 0 1 0 0 0 0 0 0	
0 0 7936 0 1 0 0 1 0 0 0	
0 0 0 0 1 0 0 0 0 0 0	
0 0 0 0 1 0 0 1 0 0 0	
0 0 0 0 0 0 0 0 0 0 0	
0 0 0 0 0 0 0 1 0 0 0	
0 0 0 0 0 0 0 0 0 0 0	
0 0 0 0 0 0 0 1 0 0 0	
0 0 0 0 0 0 0 0 0 0 0	
0 0 0 0 0 0 0 1 0 0 0	
0 0 0 0 0 1 0 0 0 0 0	
0 0 0 0 0 1 0 1 0 0 0	
0 0 0 0 0 0 0 0 x 0 0	
0 0 0 0 0 0 0 1 x 0 0	
0 0 0 0 0 0 0 0 x 0 0	
0 0 0 0 0 0 0 1 x 0 0	
0 0 0 0 0 0 0 0 x 0 0	
0 0 0 0 0 0 0 1 x 0 0	
0 0 0 0 0 0 0 0 x 0 0	
0 0 0 0 0 0 0 1 x 0 0	
0 0 0 0 0 0 0 0 x 0 0	
0 0 0 0 0 0 0 1 x 0 0	
0 0 0 0 0 0 0 0 x 0 0	
0 0 0 0 0 0 0 1 x 0 0	
0 0 0 0 0 0 0 0 x 0 0	
0 0 0 0 0 0 0 1 x 0 0	
0 0 0 0 0 0 0 0 x 0 0	
0 0 0 0 0 0 0 1 x 0 0	
0 0 0 0 0 0 0 0 x 0 0	
0 0 0 0 0 0 0 1 x 0 0	
0 0 0 0 0 0 0 0 x 0 0	
0 0 0 0 0 0 0 1 x 0 0	
0 0 0 0 0 0 0 0 x 0 0	
0 0 0 0 0 0 0 1 x 0 0	
0 0 0 0 0 0 0 0 x 0 0	
0 0 0 0 0 0 0 1 x 0 0	
0 0 0 0 0 0 0 0 x 0 0	
0 0 0 0 0 0 0 1 x 0 0	
0 0 0 0 0 0 0 0 x 0 0	
0 0 0 0 0 0 0 1 x 0 0	
0 0 0 0 0 0 0 0 x 0 0	
0 0 0 0 0 0 0 1 x 0 0	
0 0 0 0 0 0 0 0 x 0 0	
0 0 0 0 0 0 0 1 x 0 0	
0 0 0 0 0 0 0 0 x 0 0	
0 0 0 0 0 0 0 1 x 0 0	
0 0 0 0 0 0 0 0 x 0 0	
0 0 0 0 0 0 0 1 x 0 0	
0 0 0 0 0 0 0 0 x 0 0	
0 0 0 0 0 0 0 1 x 0 0	
0 0 0 0 0 0 0 0 x 0 0	
0 0 0 0 0 0 0 1 x 0 0	
0 0 0 0 0 0 0 0 x 0 0	
0 0 0 0 0 0 0 1 x 0 0	
0 0 0 0 0 0 0 0 x 0 0	
0 0 0 0 0 0 0 1 x 0 0	
0 0 0 0 0 0 0 0 x 0 0	
0 0 0 0 0 0 0 1 x 0 0	
0 0 0 0 0 0 0 0 x 0 0	
0 0 0 0 0 0 0 1 x 0 0	
0 0 0 0 0 0 0 0 x 0 0	
0 0 0 0 0 0 0 1 x 0 0	
0 0 0 0 0 0 0 0 x 0 0	
0 0 0 0 0 0 0 1 1 0 0	
0 0 0 0 0 0 1 0 1 0 0	
0 0 0 0 0 0 1 1 1 0 0	
0 0 0 0 0 0 0 0 1 0 0	
0 0 0 0 0 0 0 1 1 0 0	
0 0 0 0 0 0 0 0 1 0 0	
0 0 0 0 0 0 0 1 1 0 0	
0 0 0 0 0 0 0 0 1 0 0	
0 0 0 0 0 0 0 1 1 0 69	
0 0 0 0 0 0 0 0 1 0 69	
0 0 0 0 0 0 0 1 1 0 0	
0 0 0 0 0 0 0 0 1 0 0	
0 0 0 0 0 0 0 1 1 0 0	
0 0 0 0 0 0 0 0 1 0 0	
0 0 0 0 0 0 0 1 1 0 0	
0 0 0 0 0 0 0 0 1 0 0	
0 0 0 0 0 0 0 1 1 0 0	
0 0 0 0 0 0 0 0 1 0 0	
0 0 0 0 0 0 0 1 1 0 0	
0 0 0 0 0 0 0 0 1 0 0	
0 0 0 0 0 0 0 1 1 0 0	
0 0 0 0 0 0 0 0 1 0 0	
0 0 0 0 0 0 0 1 1 0 0	
0 0 0 0 0 0 0 0 1 0 0	
0 0 0 0 0 0 0 1 1 0 0	
0 0 0 0 0 0 0 0 1 0 0	
0 0 0 0 0 0 0 1 1 0 0	
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*/

/* Test case 01_P01T2:
M N progIN reset progLoad start result clk valid done output
0 0 0 0 0 0 0 0 x x x
0 0 0 0 0 0 0 1 x x x
0 0 0 1 0 0 0 0 x x x
0 0 0 1 0 0 0 1 0 0 0
0 0 0 0 0 0 0 0 0 0 0
0 0 0 0 0 0 0 1 0 0 0
0 0 0 0 0 0 0 0 0 0 0
0 0 0 0 0 0 0 1 0 0 0
0 0 0 0 0 0 0 0 0 0 0
0 0 0 0 0 0 0 1 0 0 0
0 0 0 0 0 0 0 0 0 0 0
0 0 0 0 0 0 0 1 0 0 0
0 0 0 0 0 0 0 0 0 0 0
0 0 0 0 0 0 0 1 0 0 0
0 0 0 0 0 0 0 0 0 0 0
0 0 0 0 0 0 0 1 0 0 0
0 0 0 0 0 0 0 0 0 0 0
0 0 0 0 0 0 0 1 0 0 0
0 0 0 0 0 0 0 0 0 0 0
0 0 0 0 0 0 0 1 0 0 0
0 0 0 0 0 0 0 0 0 0 0
0 0 0 0 0 0 0 1 0 0 0
0 0 0 0 0 0 0 0 0 0 0
0 0 0 0 0 0 0 1 0 0 0
0 0 0 0 0 0 0 0 0 0 0
0 0 0 0 0 0 0 1 0 0 0
0 0 0 0 0 0 0 0 0 0 0
0 0 0 0 0 0 0 1 0 0 0
0 0 0 0 0 0 0 0 0 0 0
0 0 0 0 0 0 0 1 0 0 0
0 0 0 0 0 0 0 0 0 0 0
0 0 0 0 0 0 0 1 0 0 0
0 0 0 0 0 0 0 0 0 0 0
0 0 0 0 0 0 0 1 0 0 0
0 0 0 0 0 0 0 0 0 0 0
0 0 0 0 0 0 0 1 0 0 0
0 0 0 0 0 0 0 0 0 0 0
0 0 0 0 0 0 0 1 0 0 0
0 0 0 0 0 0 0 0 0 0 0
0 0 0 0 0 0 0 1 0 0 0
0 0 0 0 0 0 0 0 0 0 0
0 0 0 0 0 0 0 1 0 0 0
0 0 0 0 0 0 0 0 0 0 0
0 0 0 0 0 0 0 1 0 0 0
0 0 271 0 1 0 0 0 0 0 0
0 0 271 0 1 0 0 1 0 0 0
0 0 565 0 1 0 0 0 0 0 0
0 0 565 0 1 0 0 1 0 0 0
0 0 5888 0 1 0 0 0 0 0 0
0 0 5888 0 1 0 0 1 0 0 0
0 0 3845 0 1 0 0 0 0 0 0
0 0 3845 0 1 0 0 1 0 0 0
0 0 4352 0 1 0 0 0 0 0 0
0 0 4352 0 1 0 0 1 0 0 0
0 0 3847 0 1 0 0 0 0 0 0
0 0 3847 0 1 0 0 1 0 0 0
0 0 4352 0 1 0 0 0 0 0 0
0 0 4352 0 1 0 0 1 0 0 0
0 0 4107 0 1 0 0 0 0 0 0
0 0 4107 0 1 0 0 1 0 0 0
0 0 1024 0 1 0 0 0 0 0 0
0 0 1024 0 1 0 0 1 0 0 0
0 0 5888 0 1 0 0 0 0 0 0
0 0 5888 0 1 0 0 1 0 0 0
0 0 3331 0 1 0 0 0 0 0 0
0 0 3331 0 1 0 0 1 0 0 0
0 0 2819 0 1 0 0 0 0 0 0
0 0 2819 0 1 0 0 1 0 0 0
0 0 7936 0 1 0 0 0 0 0 0
0 0 7936 0 1 0 0 1 0 0 0
0 0 0 0 0 0 0 0 0 0 0
0 0 0 0 0 0 0 1 0 0 0
0 0 0 0 0 1 0 0 0 0 0
0 0 0 0 0 1 0 1 0 0 0
0 0 0 0 0 0 0 0 x 0 0
0 0 0 0 0 0 0 1 x 0 0
0 0 0 0 0 0 0 0 x 0 0
0 0 0 0 0 0 0 1 x 0 0
0 0 0 0 0 0 0 0 x 0 0
0 0 0 0 0 0 0 1 x 0 0
0 0 0 0 0 0 0 0 x 0 0
0 0 0 0 0 0 0 1 x 0 0
0 0 0 0 0 0 0 0 x 0 0
0 0 0 0 0 0 0 1 x 0 0
0 0 0 0 0 0 0 0 x 0 0
0 0 0 0 0 0 0 1 x 0 0
0 0 0 0 0 0 0 0 x 0 0
0 0 0 0 0 0 0 1 x 0 0
0 0 0 0 0 0 0 0 x 0 0
0 0 0 0 0 0 0 1 x 0 0
0 0 0 0 0 0 0 0 x 0 0
0 0 0 0 0 0 0 1 x 0 0
0 0 0 0 0 0 0 0 x 0 0
0 0 0 0 0 0 0 1 x 0 0
0 0 0 0 0 0 0 0 x 0 0
0 0 0 0 0 0 0 1 x 0 0
0 0 0 0 0 0 0 0 x 0 0
0 0 0 0 0 0 0 1 x 0 0
0 0 0 0 0 0 0 0 x 0 0
0 0 0 0 0 0 0 1 x 0 0
0 0 0 0 0 0 0 0 x 0 0
0 0 0 0 0 0 0 1 x 0 0
0 0 0 0 0 0 0 0 x 0 0
0 0 0 0 0 0 0 1 x 0 0
0 0 0 0 0 0 0 0 x 0 0
0 0 0 0 0 0 0 1 x 0 0
0 0 0 0 0 0 0 0 x 0 0
0 0 0 0 0 0 0 1 x 0 0
0 0 0 0 0 0 0 0 x 0 0
0 0 0 0 0 0 0 1 x 0 0
0 0 0 0 0 0 0 0 x 0 0
0 0 0 0 0 0 0 1 x 0 0
0 0 0 0 0 0 0 0 x 0 0
0 0 0 0 0 0 0 1 x 0 0
0 0 0 0 0 0 0 0 x 0 0
0 0 0 0 0 0 0 1 x 0 0
0 0 0 0 0 0 0 0 x 0 0
0 0 0 0 0 0 0 1 x 0 0
0 0 0 0 0 0 0 0 x 0 0
0 0 0 0 0 0 0 1 x 0 0
0 0 0 0 0 0 0 0 x 0 0
0 0 0 0 0 0 0 1 x 0 0
0 0 0 0 0 0 0 0 x 0 0
0 0 0 0 0 0 0 1 x 0 0
0 0 0 0 0 0 0 0 x 0 0
0 0 0 0 0 0 0 1 x 0 0
0 0 0 0 0 0 0 0 x 0 0
0 0 0 0 0 0 0 1 x 0 0
0 0 0 0 0 0 0 0 x 0 0
0 0 0 0 0 0 0 1 x 0 0
0 0 0 0 0 0 0 0 x 0 0
0 0 0 0 0 0 0 1 x 0 0
0 0 0 0 0 0 0 0 x 0 0
0 0 0 0 0 0 0 1 x 0 0
0 0 0 0 0 0 0 0 x 0 0
0 0 0 0 0 0 0 1 x 0 0
0 0 0 0 0 0 0 0 x 0 0
0 0 0 0 0 0 0 1 x 0 0
0 0 0 0 0 0 0 0 x 0 0
0 0 0 0 0 0 0 1 x 0 0
0 0 0 0 0 0 0 0 x 0 0
0 0 0 0 0 0 0 1 x 0 0
0 0 0 0 0 0 0 0 x 0 0
0 0 0 0 0 0 0 1 x 0 0
0 0 0 0 0 0 0 0 x 0 0
0 0 0 0 0 0 0 1 x 0 0
0 0 0 0 0 0 0 0 x 0 0
0 0 0 0 0 0 0 1 x 0 0
0 0 0 0 0 0 0 0 x 0 0
0 0 0 0 0 0 0 1 x 0 0
0 0 0 0 0 0 0 0 x 0 0
0 0 0 0 0 0 0 1 x 0 0
0 0 0 0 0 0 0 0 x 0 0
0 0 0 0 0 0 0 1 x 0 0
0 0 0 0 0 0 0 0 x 0 0
0 0 0 0 0 0 0 1 x 0 0
0 0 0 0 0 0 0 0 x 0 0
0 0 0 0 0 0 0 1 x 0 0
0 0 0 0 0 0 0 0 x 0 0
0 0 0 0 0 0 0 1 x 0 0
0 0 0 0 0 0 0 0 x 0 0
0 0 0 0 0 0 0 1 x 0 0
0 0 0 0 0 0 0 0 x 0 0
0 0 0 0 0 0 0 1 x 0 0
0 0 0 0 0 0 0 0 x 0 0
0 0 0 0 0 0 0 1 x 0 0
0 0 0 0 0 0 0 0 x 0 0
0 0 0 0 0 0 0 1 x 0 0
0 0 0 0 0 0 0 0 x 0 0
0 0 0 0 0 0 0 1 x 0 0
0 0 0 0 0 0 0 0 x 0 0
0 0 0 0 0 0 0 1 x 0 0
0 0 0 0 0 0 0 0 x 0 0
0 0 0 0 0 0 0 1 x 0 0
0 0 0 0 0 0 0 0 x 0 0
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*/

/* Test case 01_P01T3:
M N progIN reset progLoad start result clk valid done output
0 0 0 0 0 0 0 0 x x x
0 0 0 0 0 0 0 1 x x x
0 0 0 1 0 0 0 0 x x x
0 0 0 1 0 0 0 1 x x x
0 0 0 0 0 0 0 0 x x x
0 0 0 0 0 0 0 1 x x x
0 0 0 0 0 0 0 0 x x x
0 0 0 0 0 0 0 1 x x x
0 0 0 0 0 0 0 0 x x x
0 0 0 0 0 0 0 1 x x x
0 0 0 0 0 0 0 0 x x x
0 0 0 0 0 0 0 1 x x x
0 0 0 0 0 0 0 0 x x x
0 0 0 0 0 0 0 1 x x x
0 0 0 0 0 0 0 0 x x x
0 0 0 0 0 0 0 1 x x x
0 0 0 0 0 0 0 0 x x x
0 0 0 0 0 0 0 1 x x x
0 0 0 0 0 0 0 0 x x x
0 0 0 0 0 0 0 1 x x x
0 0 0 0 0 0 0 0 x x x
0 0 0 0 0 0 0 1 x x x
0 0 0 0 0 0 0 0 x x x
0 0 0 0 0 0 0 1 x x x
0 0 0 0 0 0 0 0 x x x
0 0 0 0 0 0 0 1 x x x
0 0 0 0 0 0 0 0 x x x
0 0 0 0 0 0 0 1 x x x
0 0 0 0 0 0 0 0 x x x
0 0 0 0 0 0 0 1 x x x
0 0 0 0 0 0 0 0 x x x
0 0 0 0 0 0 0 1 x x x
0 0 0 0 0 0 0 0 x x x
0 0 0 0 0 0 0 1 x x x
0 0 0 0 0 0 0 0 x x x
0 0 0 0 0 0 0 1 x x x
0 0 0 0 0 0 0 0 x x x
0 0 0 0 0 0 0 1 x x x
0 0 0 0 0 0 0 0 x x x
0 0 0 0 0 0 0 1 x x x
0 0 0 0 0 0 0 0 x x x
0 0 0 0 0 0 0 1 x x x
0 0 0 0 0 0 0 0 x x x
0 0 0 0 0 0 0 1 x x x
0 0 0 0 0 0 0 0 0 0 x
0 0 0 0 0 0 0 1 0 0 x
0 0 1792 0 1 0 0 0 0 0 x
0 0 1792 0 1 0 0 1 0 0 x
0 0 1536 0 1 0 0 0 0 0 x
0 0 1536 0 1 0 0 1 0 0 x
0 0 2817 0 1 0 0 0 0 0 x
0 0 2817 0 1 0 0 1 0 0 x
0 0 7936 0 1 0 0 0 0 0 x
0 0 7936 0 1 0 0 1 0 0 x
0 0 0 0 0 1 0 0 0 0 x
0 0 0 0 0 1 0 1 0 0 x
500 0 0 0 0 0 0 0 x x x
500 0 0 0 0 0 0 1 x x x
500 0 0 0 0 0 0 0 x x x
500 0 0 0 0 0 0 1 x x x
500 0 0 0 0 0 0 0 x x x
500 0 0 0 0 0 0 1 x x x
500 0 0 0 0 0 0 0 x x x
500 0 0 0 0 0 0 1 x x x
500 0 0 0 0 0 0 0 x x x
500 0 0 0 0 0 0 1 x x x
500 0 0 0 0 0 0 0 x x x
500 0 0 0 0 0 0 1 x x x
500 0 0 0 0 0 0 0 x x x
500 0 0 0 0 0 0 1 x x x
500 0 0 0 0 0 0 0 x x x
500 0 0 0 0 0 0 1 x x x
500 0 0 0 0 0 0 0 x x x
500 0 0 0 0 0 0 1 x x x
500 0 0 0 0 0 0 0 x x x
500 0 0 0 0 0 0 1 x x x
500 0 0 0 0 0 0 1 x x x
500 0 0 0 0 0 0 1 x x x
500 0 0 0 0 0 0 1 x x x
0 0 0 0 0 0 1 0 1 0 x
0 0 0 0 0 0 1 1 1 0 0
0 0 0 0 0 0 0 0 1 0 0
0 0 0 0 0 0 0 1 1 0 500
0 0 0 0 0 0 0 0 1 0 500
0 0 0 0 0 0 0 1 1 0 0
0 0 0 0 0 0 0 0 1 0 0
0 0 0 0 0 0 0 1 1 0 0
0 0 0 0 0 0 0 0 1 0 0
0 0 0 0 0 0 0 1 1 0 0
0 0 0 0 0 0 0 0 1 0 0
0 0 0 0 0 0 0 1 1 0 0
0 0 0 0 0 0 0 0 1 0 0
0 0 0 0 0 0 0 1 1 0 0
0 0 0 0 0 0 0 0 1 0 0
0 0 0 0 0 0 0 1 1 0 0
0 0 0 0 0 0 0 0 1 0 0
0 0 0 0 0 0 0 1 1 0 0
0 0 0 0 0 0 0 0 1 0 0
0 0 0 0 0 0 0 1 1 0 0
0 0 0 0 0 0 0 0 1 0 0
0 0 0 0 0 0 0 1 1 0 0
0 0 0 0 0 0 0 0 1 0 0
0 0 0 0 0 0 0 1 1 0 0
0 0 0 0 0 0 0 0 1 0 0
0 0 0 0 0 0 0 1 1 0 0
0 0 0 0 0 0 0 0 1 0 0
0 0 0 0 0 0 0 1 1 0 0
0 0 0 0 0 0 0 0 1 0 0
0 0 0 0 0 0 0 1 1 0 0
0 0 0 0 0 0 0 0 1 0 0
0 0 0 0 0 0 0 1 1 0 0
0 0 0 0 0 0 0 0 1 0 0
0 0 0 0 0 0 0 1 1 1 x
0 0 0 1 0 0 0 0 x x x
0 0 0 1 0 0 0 1 x x x
0 0 0 0 0 0 0 0 x x x
0 0 0 0 0 0 0 1 x x x
0 0 0 0 0 0 0 0 x x x
0 0 0 0 0 0 0 1 x x x
0 0 0 0 0 0 0 0 x x x
0 0 0 0 0 0 0 1 x x x
0 0 0 0 0 0 0 0 x x x
0 0 0 0 0 0 0 1 x x x
0 0 0 0 0 0 0 0 x x x
0 0 0 0 0 0 0 1 x x x
0 0 0 0 0 0 0 0 x x x
0 0 0 0 0 0 0 1 x x x
0 0 0 0 0 0 0 0 x x x
0 0 0 0 0 0 0 1 x x x
0 0 0 0 0 0 0 0 x x x
0 0 0 0 0 0 0 1 x x x
0 0 0 0 0 0 0 0 x x x
0 0 0 0 0 0 0 1 x x x
0 0 0 0 0 0 0 0 x x x
0 0 0 0 0 0 0 1 x x x
0 0 0 0 0 0 0 0 0 0 x
0 0 0 0 0 0 0 1 0 0 x
*/

/* Test case 01_P01T4:
M N progIN reset progLoad start result clk valid done output
0 0 0 0 0 0 0 0 x x x
0 0 0 0 0 0 0 1 x x x
0 0 0 1 0 0 0 0 x x x
0 0 0 1 0 0 0 1 0 0 0
0 0 0 0 0 0 0 0 0 0 0
0 0 0 0 0 0 0 1 0 0 0
0 0 0 0 0 0 0 0 0 0 0
0 0 0 0 0 0 0 1 0 0 0
0 0 0 0 0 0 0 0 0 0 0
0 0 0 0 0 0 0 1 0 0 0
0 0 0 0 0 0 0 0 0 0 0
0 0 0 0 0 0 0 1 0 0 0
0 0 0 0 0 0 0 0 0 0 0
0 0 0 0 0 0 0 1 0 0 0
0 0 0 0 0 0 0 0 0 0 0
0 0 0 0 0 0 0 1 0 0 0
0 0 0 0 0 0 0 0 0 0 0
0 0 0 0 0 0 0 1 0 0 0
0 0 0 0 0 0 0 0 0 0 0
0 0 0 0 0 0 0 1 0 0 0
0 0 0 0 0 0 0 0 0 0 0
0 0 0 0 0 0 0 1 0 0 0
0 0 0 0 0 0 0 0 0 0 0
0 0 0 0 0 0 0 1 0 0 0
0 0 0 0 0 0 0 0 0 0 0
0 0 0 0 0 0 0 1 0 0 0
0 0 0 0 0 0 0 0 0 0 0
0 0 0 0 0 0 0 1 0 0 0
0 0 0 0 0 0 0 0 0 0 0
0 0 0 0 0 0 0 1 0 0 0
0 0 0 0 0 0 0 0 0 0 0
0 0 0 0 0 0 0 1 0 0 0
0 0 0 0 0 0 0 0 0 0 0
0 0 0 0 0 0 0 1 0 0 0
0 0 0 0 0 0 0 0 0 0 0
0 0 0 0 0 0 0 1 0 0 0
0 0 0 0 0 0 0 0 0 0 0
0 0 0 0 0 0 0 1 0 0 0
0 0 0 0 0 0 0 0 0 0 0
0 0 0 0 0 0 0 1 0 0 0
0 0 0 0 0 0 0 0 0 0 0
0 0 0 0 0 0 0 1 0 0 0
0 0 0 0 0 0 0 0 0 0 0
0 0 0 0 0 0 0 1 0 0 0
0 0 271 0 1 0 0 0 0 0 0
0 0 271 0 1 0 0 1 0 0 0
0 0 7424 0 1 0 0 0 0 0 0
0 0 7424 0 1 0 0 1 0 0 0
0 0 3328 0 1 0 0 0 0 0 0
0 0 3328 0 1 0 0 1 0 0 0
0 0 257 0 1 0 0 0 0 0 0
0 0 257 0 1 0 0 1 0 0 0
0 0 3330 0 1 0 0 0 0 0 0
0 0 3330 0 1 0 0 1 0 0 0
0 0 455 0 1 0 0 0 0 0 0
0 0 455 0 1 0 0 1 0 0 0
0 0 7424 0 1 0 0 0 0 0 0
0 0 7424 0 1 0 0 1 0 0 0
0 0 3337 0 1 0 0 0 0 0 0
0 0 3337 0 1 0 0 1 0 0 0
0 0 2817 0 1 0 0 0 0 0 0
0 0 2817 0 1 0 0 1 0 0 0
0 0 7936 0 1 0 0 0 0 0 0
0 0 7936 0 1 0 0 1 0 0 0
0 0 0 0 0 0 0 0 0 0 0
0 0 0 0 0 0 0 1 0 0 0
0 0 0 0 0 0 0 0 0 0 0
0 0 0 0 0 0 0 1 0 0 0
0 0 0 0 0 0 0 0 0 0 0
0 0 0 0 0 0 0 1 0 0 0
0 0 0 0 0 0 0 0 0 0 0
0 0 0 0 0 0 0 1 0 0 0
0 0 0 0 0 1 0 0 0 0 0
0 0 0 0 0 1 0 1 0 0 0
0 0 0 0 0 0 0 0 x 0 0
0 0 0 0 0 0 0 1 x 0 0
0 0 0 0 0 0 0 0 x 0 0
0 0 0 0 0 0 0 1 x 0 0
0 0 0 0 0 0 0 0 x 0 0
0 0 0 0 0 0 0 1 x 0 0
0 0 0 0 0 0 0 0 x 0 0
0 0 0 0 0 0 0 1 x 0 0
0 0 0 0 0 0 0 0 x 0 0
0 0 0 0 0 0 0 1 x 0 0
0 0 0 0 0 0 0 0 x 0 0
0 0 0 0 0 0 0 1 x 0 0
0 0 0 0 0 0 0 0 x 0 0
0 0 0 0 0 0 0 1 x 0 0
0 0 0 0 0 0 0 0 x 0 0
0 0 0 0 0 0 0 1 x 0 0
0 0 0 0 0 0 0 0 x 0 0
0 0 0 0 0 0 0 1 x 0 0
0 0 0 0 0 0 0 0 x 0 0
0 0 0 0 0 0 0 1 x 0 0
0 0 0 0 0 0 0 0 x 0 0
0 0 0 0 0 0 0 1 x 0 0
0 0 0 0 0 0 0 0 x 0 0
0 0 0 0 0 0 0 1 x 0 0
0 0 0 0 0 0 0 0 x 0 0
0 0 0 0 0 0 0 1 x 0 0
0 0 0 0 0 0 0 0 x 0 0
0 0 0 0 0 0 0 1 x 0 0
0 0 0 0 0 0 0 0 x 0 0
0 0 0 0 0 0 0 1 x 0 0
0 0 0 0 0 0 0 0 x 0 0
0 0 0 0 0 0 0 1 x 0 0
0 0 0 0 0 0 0 0 x 0 0
0 0 0 0 0 0 0 1 x 0 0
0 0 0 0 0 0 0 0 x 0 0
0 0 0 0 0 0 0 1 x 0 0
0 0 0 0 0 0 0 0 x 0 0
0 0 0 0 0 0 0 1 x 0 0
0 0 0 0 0 0 0 0 x 0 0
0 0 0 0 0 0 0 1 x 0 0
0 0 0 0 0 0 0 0 x 0 0
0 0 0 0 0 0 0 1 x 0 0
0 0 0 0 0 0 0 0 x 0 0
0 0 0 0 0 0 0 1 x 0 0
0 0 0 0 0 0 0 0 x 0 0
0 0 0 0 0 0 0 1 x 0 0
0 0 0 0 0 0 0 0 x 0 0
0 0 0 0 0 0 0 1 x 0 0
0 0 0 0 0 0 0 0 x 0 0
0 0 0 0 0 0 0 1 x 0 0
0 0 0 0 0 0 0 0 x 0 0
0 0 0 0 0 0 0 1 x 0 0
0 0 0 0 0 0 0 0 x 0 0
0 0 0 0 0 0 0 1 x 0 0
0 0 0 0 0 0 0 0 x 0 0
0 0 0 0 0 0 0 1 x 0 0
0 0 0 0 0 0 0 0 x 0 0
0 0 0 0 0 0 0 1 x 0 0
0 0 0 0 0 0 0 0 x 0 0
0 0 0 0 0 0 0 1 x 0 0
0 0 0 0 0 0 0 0 x 0 0
0 0 0 0 0 0 0 1 x 0 0
0 0 0 0 0 0 0 0 x 0 0
0 0 0 0 0 0 0 1 x 0 0
0 0 0 0 0 0 0 0 x 0 0
0 0 0 0 0 0 0 1 x 0 0
0 0 0 0 0 0 0 0 x 0 0
0 0 0 0 0 0 0 1 x 0 0
0 0 0 0 0 0 0 0 x 0 0
0 0 0 0 0 0 0 1 x 0 0
0 0 0 0 0 0 0 0 x 0 0
0 0 0 0 0 0 0 1 x 0 0
0 0 0 0 0 0 0 0 x 0 0
0 0 0 0 0 0 0 1 x 0 0
0 0 0 0 0 0 0 0 x 0 0
0 0 0 0 0 0 0 1 x 0 0
0 0 0 0 0 0 0 0 x 0 0
0 0 0 0 0 0 0 1 x 0 0
0 0 0 0 0 0 0 0 x 0 0
0 0 0 0 0 0 0 1 x 0 0
0 0 0 0 0 0 0 0 x 0 0
0 0 0 0 0 0 0 1 x 0 0
0 0 0 0 0 0 0 0 x 0 0
0 0 0 0 0 0 0 1 x 0 0
0 0 0 0 0 0 0 0 x 0 0
0 0 0 0 0 0 0 1 x 0 0
0 0 0 0 0 0 0 0 x 0 0
0 0 0 0 0 0 0 1 x 0 0
0 0 0 0 0 0 0 0 x 0 0
0 0 0 0 0 0 0 1 x 0 0
0 0 0 0 0 0 0 0 x 0 0
0 0 0 0 0 0 0 1 x 0 0
0 0 0 0 0 0 0 0 x 0 0
0 0 0 0 0 0 0 1 x 0 0
0 0 0 0 0 0 0 0 x 0 0
0 0 0 0 0 0 0 1 x 0 0
0 0 0 0 0 0 0 0 x 0 0
0 0 0 0 0 0 0 1 x 0 0
0 0 0 0 0 0 0 0 x 0 0
0 0 0 0 0 0 0 1 x 0 0
0 0 0 0 0 0 0 0 x 0 0
0 0 0 0 0 0 0 1 x 0 0
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*/

/* Test case 01_P01T5:
M N progIN reset progLoad start result clk valid done output
0 0 0 0 0 0 0 0 x x x
0 0 0 0 0 0 0 1 x x x
0 0 0 1 0 0 0 0 0 0 0
0 0 0 1 0 0 0 1 0 0 0
0 0 0 0 0 0 0 0 0 0 0
0 0 0 0 0 0 0 1 0 0 0
0 0 0 0 0 0 0 0 0 0 0
0 0 0 0 0 0 0 1 0 0 0
0 0 0 0 0 0 0 0 0 0 0
0 0 0 0 0 0 0 1 0 0 0
0 0 0 0 0 0 0 0 0 0 0
0 0 0 0 0 0 0 1 0 0 0
0 0 0 0 0 0 0 0 0 0 0
0 0 0 0 0 0 0 1 0 0 0
0 0 0 0 0 0 0 0 0 0 0
0 0 0 0 0 0 0 1 0 0 0
0 0 0 0 0 0 0 0 0 0 0
0 0 0 0 0 0 0 1 0 0 0
0 0 0 0 0 0 0 0 0 0 0
0 0 0 0 0 0 0 1 0 0 0
0 0 0 0 0 0 0 0 0 0 0
0 0 0 0 0 0 0 1 0 0 0
0 0 0 0 0 0 0 0 0 0 0
0 0 0 0 0 0 0 1 0 0 0
0 0 0 0 0 0 0 0 0 0 0
0 0 0 0 0 0 0 1 0 0 0
0 0 0 0 0 0 0 0 0 0 0
0 0 0 0 0 0 0 1 0 0 0
0 0 0 0 0 0 0 0 0 0 0
0 0 0 0 0 0 0 1 0 0 0
0 0 0 0 0 0 0 0 0 0 0
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*/

/* Test case 01_P01T6:
M N progIN reset progLoad start result clk valid done output
0 0 0 0 0 0 0 0 0 0 0
0 0 0 0 0 0 0 1 0 0 0
0 0 0 1 0 0 0 0 0 0 0
0 0 0 1 0 0 0 1 0 0 0
0 0 0 0 0 0 0 0 0 0 0
0 0 0 0 0 0 0 1 0 0 0
0 0 0 0 0 0 0 0 0 0 0
0 0 0 0 0 0 0 1 0 0 0
0 0 0 0 0 0 0 0 0 0 0
0 0 0 0 0 0 0 1 0 0 0
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*/

/* Test case 01_P01T7:
M N progIN reset progLoad start result clk valid done output
0 0 0 0 0 0 0 0 0 0 0
0 0 0 0 0 0 0 1 0 0 0
0 0 0 1 0 0 0 0 0 0 0
0 0 0 1 0 0 0 1 0 0 0
0 0 0 0 0 0 0 0 0 0 0
0 0 0 0 0 0 0 1 0 0 0
0 0 0 0 0 0 0 0 0 0 0
0 0 0 0 0 0 0 1 0 0 0
0 0 0 0 0 0 0 0 0 0 0
0 0 0 0 0 0 0 1 0 0 0
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*/
