// Digital circuit ALU.dig as structural Verilog
module ALU (
  input  [7:0] A,
  input  [7:0] B,
  input  [3:0] op,
  output [7:0] ans
);

  wire or_2_out;
  wire [7:0] A_B, A_lt__lt_B, A_t, AND, barrelshifter_1_out, DIFF, DIV, MOD, MUL, OR, SUM, XOR;

  assign AND = A & B;  // And and_1, 8 bits wide
  assign OR = A | B;  // Or or_1, 8 bits wide
  assign XOR = A ^ B;  // XOr xor_1, 8 bits wide
  Add #(.Bits(8)) add_1 (.a(A), .b(B), .c_i(1'b0), .s(SUM));  // open: c_o
  Sub #(.Bits(8)) sub_1 (.a(A), .b(B), .c_i(1'b0), .s(DIFF));  // open: c_o
  Mul #(.Bits(4)) mul_1 (.a(A[3:0]), .b(B[3:0]), .mul(MUL));
  Div #(.Bits(8)) divide (.a(A), .b(B), .q(DIV));  // open: r
  Div #(.Bits(8)) u_mod (.a(A), .b(B), .q(MOD));  // open: r
  EXPO expo_1 (.B(B[2:0]), .A(A[2:0]), .A_B(A_B));
  assign A_t = ~A;  // Not not_1, 8 bits wide
  Multiplexer #(.Selector_Bits(4), .Bits(8)) multiplexer_1 (
    .sel(op), .in_0({8{1'b0}}), .in_1(SUM), .in_2(DIFF), .in_3(MUL), .in_4(DIV), .in_5(MOD), .in_6(A_B),
    .in_7({8{1'b0}}), .in_8(A_t), .in_9(AND), .in_10(OR), .in_11(XOR), .in_12(A_lt__lt_B), .in_13({8{1'b0}}),
    .in_14({8{1'b0}}), .in_15({8{1'b0}}), .out(ans));
  BarrelShifter #(.Bits(8), .barrelShifterMode("arithmetic")) barrelshifter_1 (
    .in(A), .shift(B[3:0]), .out(barrelshifter_1_out));
  or or_2 (or_2_out, B[4], B[5], B[6], B[7]);
  Multiplexer #(.Bits(8)) multiplexer_2 (
    .sel(or_2_out), .in_0(barrelshifter_1_out), .in_1({8{1'b0}}), .out(A_lt__lt_B));

  // Other names for the same wires on the sheet: accA[7:0] = A; accB[7:0] = B
endmodule
