// Digital circuit EXPO.dig as structural Verilog
module EXPO (
  input  [2:0] B,
  input  [2:0] A,
  output [7:0] A_B
);

  wire and_1_out, and_2_out, and_3_out, and_4_out, and_5_out, and_6_out, and_7_out, and_8_out, and_9_out,
       and_10_out, and_11_out, and_12_out, and_13_out, and_14_out, and_15_out, and_16_out, and_17_out,
       and_18_out, and_19_out, and_20_out, and_21_out, and_22_out, and_23_out, and_24_out, and_25_out,
       and_26_out, and_27_out, and_28_out, and_29_out, and_30_out, and_31_out, and_32_out, and_33_out,
       and_34_out, and_35_out, and_36_out, and_37_out, and_38_out, and_39_out, and_40_out, and_41_out,
       and_42_out, and_43_out, and_44_out, and_45_out, and_46_out, and_47_out, and_48_out, and_49_out,
       and_50_out, and_51_out, and_52_out, and_53_out, and_54_out, and_55_out, or_3_out, or_4_out, or_5_out,
       or_11_out, or_12_out;

  and and_1 (and_1_out, A[2], A[1], ~A[0], ~B[2], A[1]);  // And
  and and_2 (and_2_out, ~A[2], A[1], B[2], A[1], B[0]);  // And
  and and_3 (and_3_out, ~A[2], A[1], A[0], B[2], ~A[1]);  // And
  and and_4 (and_4_out, A[1], A[0], B[2], A[1]);
  and and_5 (and_5_out, A[2], A[1], A[0], B[2], B[0]);
  and and_6 (and_6_out, A[2], ~A[1], A[0], ~B[2], A[1]);  // And
  and and_7 (and_7_out, A[1], ~A[0], ~B[2], A[1], B[0]);  // And
  and and_8 (and_8_out, A[2], A[0], B[2], A[1], ~B[0]);  // And
  and and_9 (and_9_out, A[1], A[0], B[2], A[1], B[0]);
  and and_10 (and_10_out, ~A[2], A[1], A[0], A[1]);  // And
  and and_11 (and_11_out, and_1_out, B[0]);
  and and_12 (and_12_out, and_3_out, B[0]);
  or or_1 (A_B[7], and_11_out, and_2_out, and_12_out, and_4_out, and_5_out);
  or or_2 (A_B[3], and_6_out, and_7_out, and_8_out, and_9_out, and_10_out);
  and and_13 (and_13_out, A[2], ~A[1], A[0], B[2], ~A[1]);  // And
  and and_14 (and_14_out, A[2], A[1], ~A[0], B[2], ~A[1]);  // And
  and and_15 (and_15_out, ~A[2], A[1], B[2], A[1], ~B[0]);  // And
  and and_16 (and_16_out, ~A[2], A[1], A[0], B[2], ~A[1]);  // And
  and and_17 (and_17_out, A[2], ~A[1], A[0], B[2], ~B[0]);  // And
  and and_18 (and_18_out, A[2], A[1], A[0], A[1], B[0]);
  and and_19 (and_19_out, A[2], ~B[2], A[1], B[0]);  // And
  and and_20 (and_20_out, A[1], A[0], B[2], ~B[0]);  // And
  and and_21 (and_21_out, A[2], ~A[1], A[0], B[2], ~A[1]);  // And
  and and_22 (and_22_out, A[1], ~A[0], ~B[2], A[1], ~B[0]);  // And
  and and_23 (and_23_out, A[2], ~A[1], A[0], A[1], B[0]);  // And
  and and_24 (and_24_out, A[2], ~B[2], ~A[1], B[0]);  // And
  and and_25 (and_25_out, A[2], A[1], A[0], A[1], B[0]);
  and and_26 (and_26_out, A[2], A[1], A[0], B[2], B[0]);
  and and_27 (and_27_out, and_13_out, B[0]);
  and and_28 (and_28_out, and_14_out, B[0]);
  and and_29 (and_29_out, and_16_out, B[0]);
  and and_30 (and_30_out, and_21_out, B[0]);
  or or_3 (or_3_out, and_27_out, and_28_out, and_15_out, and_29_out, and_17_out);
  or or_4 (or_4_out, and_18_out, and_19_out, and_20_out);
  or or_5 (or_5_out, and_30_out, and_22_out, and_23_out, and_24_out, and_25_out);
  or or_6 (A_B[6], or_3_out, or_4_out);
  or or_7 (A_B[2], or_5_out, and_26_out);
  and and_31 (and_31_out, ~A[2], A[1], B[2], ~A[1], B[0]);  // And
  and and_32 (and_32_out, A[2], A[1], ~B[2], A[1], ~B[0]);  // And
  and and_33 (and_33_out, A[2], ~A[1], A[0], A[1], B[0]);  // And
  and and_34 (and_34_out, A[2], ~A[1], A[0], B[2], ~B[0]);  // And
  and and_35 (and_35_out, A[2], A[1], A[0], B[2], B[0]);
  and and_36 (and_36_out, ~A[2], A[1], A[0], B[2], ~A[1]);  // And
  and and_37 (and_37_out, A[1], ~B[2], ~A[1], B[0]);  // And
  and and_38 (and_38_out, A[1], A[0], B[2], A[1], B[0]);
  and and_39 (and_39_out, A[1], A[0], ~B[2], A[1], B[0]);  // And
  and and_40 (and_40_out, A[2], A[1], A[0], B[2], B[0]);
  and and_41 (and_41_out, and_36_out, B[0]);
  or or_8 (A_B[5], and_31_out, and_32_out, and_33_out, and_34_out, and_35_out);
  or or_9 (A_B[1], and_41_out, and_37_out, and_38_out, and_39_out, and_40_out);
  and and_42 (and_42_out, A[2], A[1], ~A[0], B[2], ~A[1]);  // And
  and and_43 (and_43_out, A[2], A[1], ~A[0], ~B[2], A[1]);  // And
  and and_44 (and_44_out, A[2], ~A[1], ~B[2], A[1], B[0]);  // And
  and and_45 (and_45_out, ~A[2], A[1], A[0], B[2], ~A[1]);  // And
  and and_46 (and_46_out, A[2], ~A[1], A[0], B[2], ~B[0]);  // And
  and and_47 (and_47_out, A[1], B[2], ~A[1], ~B[0]);  // And
  and and_48 (and_48_out, A[1], A[0], ~B[2], A[1], B[0]);  // And
  and and_49 (and_49_out, A[1], A[0], B[2], ~B[0]);  // And
  and and_50 (and_50_out, A[2], A[1], A[0], B[2], B[0]);
  and and_51 (and_51_out, A[2], A[0], A[1]);
  and and_52 (and_52_out, ~B[2], ~A[1], ~B[0]);  // And
  and and_53 (and_53_out, and_42_out, B[0]);
  and and_54 (and_54_out, and_43_out, B[0]);
  and and_55 (and_55_out, and_45_out, B[0]);
  or or_10 (A_B[0], and_52_out, A[0]);
  or or_11 (or_11_out, and_53_out, and_54_out, and_44_out, and_55_out, and_46_out);
  or or_12 (or_12_out, and_47_out, and_48_out, and_49_out, and_50_out, and_51_out);
  or or_13 (A_B[4], or_11_out, or_12_out);

  assign B[1] = A[1];

  // Other names for the same wires on the sheet: X0 = A_B[0]; X1 = A_B[1]; X2 = A_B[2]; X3 = A_B[3]; X4 = A_B[4];
  //   X5 = A_B[5]; X6 = A_B[6]; X7 = A_B[7]

  // Notes on the sheet:
  //   x7
  //   x3
  //   x6
  //   x2
  //   x5
  //   x1
  //   x4
  //   x0
  //   IN-OUT
endmodule
