// Digital circuit MOVE.dig as structural Verilog
module MOVE (
  input  [7:0] accA,
  input  [7:0] accB,
  input  [7:0] regC,
  input  [4:0] opcode,
  input  [7:0] operand,
  input  [7:0] rRAM_operand,
  input  [7:0] pRAM_operand,
  input  [7:0] M,
  input  [7:0] N,
  output [7:0] val,
  output enA,
  output enB,
  output enC,
  output en_rRAM
);

  wire _1, _2, _3, _4, _5, _6, _7, _8, _9, _10, or_1_out, or_2_out, or_3_out;
  wire [3:0] priorityencoder_1_num;

  Decoder #(.Selector_Bits(4)) decoder_1 (
    .sel(opcode[3:0]), .out_1(_1), .out_2(_2), .out_3(_3), .out_4(_4), .out_5(_5), .out_6(_6), .out_7(_7),
    .out_8(_8), .out_9(_9), .out_10(_10), .out_11(en_rRAM));  // open: out_0, out_12, out_13, out_14, out_15
  PriorityEncoder #(.Selector_Bits(4)) priorityencoder_1 (
    .in0(1'b0), .in1(_1), .in2(_2), .in3(_3), .in4(_4), .in5(_5), .in6(_6), .in7(_7), .in8(_8), .in9(_9),
    .in10(_10), .in11(en_rRAM), .in12(1'b0), .in13(1'b0), .in14(1'b0), .in15(1'b0),
    .num(priorityencoder_1_num));  // open: any
  or or_1 (or_1_out, _1, _3, _6, _9, _10);
  or or_2 (or_2_out, _2, _4);
  or or_3 (or_3_out, _5, _7, _8);
  Multiplexer multiplexer_1 (.sel(opcode[4]), .in_0(or_1_out), .in_1(1'b0), .out(enA));
  Multiplexer multiplexer_2 (.sel(opcode[4]), .in_0(or_2_out), .in_1(1'b0), .out(enB));
  Multiplexer multiplexer_3 (.sel(opcode[4]), .in_0(or_3_out), .in_1(1'b0), .out(enC));
  Multiplexer #(.Selector_Bits(4), .Bits(8)) multiplexer_4 (
    .sel(priorityencoder_1_num), .in_0({8{1'b0}}), .in_1(operand), .in_2(operand), .in_3(accB), .in_4(accA),
    .in_5(accA), .in_6(regC), .in_7(M), .in_8(N), .in_9(pRAM_operand), .in_10(rRAM_operand), .in_11(accA),
    .in_12({8{1'b0}}), .in_13({8{1'b0}}), .in_14({8{1'b0}}), .in_15({8{1'b0}}), .out(val));
  // Pins of 1 and 8 bits meet at val

  // Other names for the same wires on the sheet: _11 = en_rRAM; frontbit = opcode[4]

  // Notes on the sheet:
  //   DEMUX
  //   INPUT
  //   MUX
  //   OUTPUT
endmodule
