// Digital circuit draft_01.dig as structural Verilog
module draft_01 (
  input  [7:0] M,
  input  [7:0] N,
  input  [12:0] progIN,
  input  start,
  input  reset,
  input  progLoad,
  input  result,
  input  clk,
  output [7:0] out_9,
  output [7:0] out_10,
  output [7:0] out_11,
  output [7:0] out_12,
  output valid,
  output done,
  output [12:0] \output ,
  output [7:0] cnt,
  output [7:0] r_cnt
);

  wire driver_2_out, driver_3_out, driver_4_out, driver_5_out, eq, eq_t, gr, gt, isprime_1_z, le, lt,
       multiplexer_5_out, multiplexer_6_out, multiplexer_13_out, multiplexer_14_out, multiplexer_18_out,
       multiplexer_19_out, not_1_out, or_1_out, or_2_out, or_3_out, or_4_out, or_5_out, or_6_out, or_7_out,
       or_8_out, or_9_out, or_10_out, or_11_out, P_0, P_1, P_2, P_3, P_a, P_b, pc, priorityencoder_2_num,
       Q_0, Q_1, Q_2, Q_3, Q_4, Q_5, Q_6, Q_7, Q_8, Q_9, Q_10, Q_11, Q_12, Q_13, Q_14, Q_15, Q_16, Q_17,
       Q_18, Q_19, Q_20, Q_21, Q_22, Q_23, Q_24, Q_25, Q_26, Q_27, Q_28, Q_29, Q_30, Q_31, Q_a, Q_b, Q_c,
       Q_d, Q_d_op, Q_d_plus__op, Q_e, r_cnt_eq_16, r_cnt_eq_cnt, r_cnt_gt_16, r_cnt_gt_cnt, r_cnt_lt_16,
       r_cnt_lt_cnt, res_cnt_eq_16, res_cnt_gt_16, res_cnt_lt_16, result_t, start_t, undriven_3;
  wire [1:0] driver_1_out, multiplexer_1_out, multiplexer_2_out, multiplexer_7_out, multiplexer_8_out,
       priorityencoder_3_num;
  wire [2:0] priorityencoder_1_num;
  wire [4:0] opcode;
  wire [7:0] ALU_result_t, multiplexer_15_out, multiplexer_16_out, operand, pRAM_operand, res_cnt;
  wire [7:1] undriven, undriven_2;
  wire [12:0] multiplexer_3_out, multiplexer_4_out, multiplexer_10_out, multiplexer_11_out, rRAM_operand;
  wire [12:8] pRAM_2_d2;

  Decoder #(.Selector_Bits(5)) decoder_1 (
    .sel({Q_a, Q_b, Q_c, Q_d, Q_e}), .out_0(Q_0), .out_1(Q_1), .out_2(Q_2), .out_3(Q_3), .out_4(Q_4),
    .out_5(Q_5), .out_6(Q_6), .out_7(Q_7), .out_8(Q_8), .out_9(Q_9), .out_10(Q_10), .out_11(Q_11),
    .out_12(Q_12), .out_13(Q_13), .out_14(Q_14), .out_15(Q_15), .out_16(Q_16), .out_17(Q_17), .out_18(Q_18),
    .out_19(Q_19), .out_20(Q_20), .out_21(Q_21), .out_22(Q_22), .out_23(Q_23), .out_24(Q_24), .out_25(Q_25),
    .out_26(Q_26), .out_27(Q_27), .out_28(Q_28), .out_29(Q_29), .out_30(Q_30), .out_31(Q_31));
  or or_1 (or_1_out, Q_1, Q_2);
  assign driver_1_out[0] = Q_5 ? pc : 1'bz;  // Driver driver_1
  Multiplexer multiplexer_1 (.sel(Q_2), .in_0(cnt[0]), .in_1(r_cnt[0]), .out(multiplexer_1_out[0]));
  or or_2 (or_2_out, Q_4, Q_16);
  Multiplexer multiplexer_2 (.sel(Q_4), .in_0(operand[0]), .in_1(r_cnt[0]), .out(multiplexer_2_out[0]));
  D_FF d_ff_1 (.D(start), .C(clk), .Q(start_t));  // open: nQ
  D_FF d_ff_2 (.D(result), .C(clk), .Q(result_t));  // open: nQ
  Multiplexer multiplexer_3 (.sel(Q_2), .in_0(progIN[0]), .in_1(1'b0), .out(multiplexer_3_out[0]));
  Multiplexer multiplexer_4 (.sel(Q_4), .in_0(out_9[0]), .in_1(1'b0), .out(multiplexer_4_out[0]));
  RAMDualAccess #(.Bits(13)) pRAM (
    .str(or_1_out), .C(clk), .ld(1'b0), .A1(multiplexer_1_out), .Din1(multiplexer_3_out), .A2(driver_1_out),
    .D2({opcode, operand}));  // open: D1
  RAMDualAccess #(.Bits(13)) rRAM (
    .str(or_2_out), .C(clk), .ld(1'b0), .A1(multiplexer_2_out), .Din1(multiplexer_4_out), .D2(\output ));  // open: A2, D1
  Multiplexer #(.Selector_Bits(5)) multiplexer_5 (
    .sel({Q_a, Q_b, Q_c, Q_d, Q_e}), .in_0(reset), .in_1(1'b0), .in_2(1'b1), .in_3(1'b0), .in_4(1'b0),
    .in_5(Q_d_plus__op), .in_6(1'b1), .in_7(1'b1), .in_8(1'b1), .in_9(1'b1), .in_10(1'b1), .in_11(1'b1),
    .in_12(1'b1), .in_13(1'b1), .in_14(1'b1), .in_15(1'b1), .in_16(1'b1), .in_17(1'b1), .in_18(1'b1),
    .in_19(1'b1), .in_20(1'b1), .in_21(1'b1), .in_22(1'b1), .in_23(1'b1), .in_24(1'b1), .in_25(1'b1),
    .in_26(1'b0), .in_27(1'b0), .in_28(reset), .in_29(1'b0), .in_30(1'b0), .in_31(1'b0),
    .out(multiplexer_5_out));
  D_FF d_ff_3 (.D(multiplexer_5_out), .C(clk), .Q(Q_e));  // open: nQ
  Multiplexer #(.Selector_Bits(5)) multiplexer_6 (
    .sel({Q_a, Q_b, Q_c, Q_d, Q_e}), .in_0(reset), .in_1(1'b0), .in_2(1'b1), .in_3(1'b0), .in_4(1'b0),
    .in_5(Q_d_plus__op), .in_6(1'b1), .in_7(1'b1), .in_8(1'b1), .in_9(1'b1), .in_10(1'b1), .in_11(1'b1),
    .in_12(1'b1), .in_13(1'b1), .in_14(1'b1), .in_15(1'b1), .in_16(1'b1), .in_17(1'b1), .in_18(1'b1),
    .in_19(1'b1), .in_20(1'b1), .in_21(1'b1), .in_22(1'b1), .in_23(1'b1), .in_24(1'b1), .in_25(1'b1),
    .in_26(1'b0), .in_27(1'b0), .in_28(reset), .in_29(1'b0), .in_30(1'b0), .in_31(1'b0),
    .out(multiplexer_6_out));
  or or_3 (or_3_out, Q_1, Q_2);
  Multiplexer multiplexer_7 (.sel(Q_2), .in_0(cnt[0]), .in_1(r_cnt[0]), .out(multiplexer_7_out[0]));
  or or_4 (or_4_out, Q_4, Q_16);
  Multiplexer multiplexer_8 (.sel(Q_4), .in_0(operand[0]), .in_1(r_cnt[0]), .out(multiplexer_8_out[0]));
  Multiplexer multiplexer_9 (.sel(Q_3), .in_0(Q_28), .in_1(1'b0), .out(valid));
  D_FF d_ff_4 (.D(multiplexer_6_out), .C(clk), .Q(Q_e));  // open: nQ
  Multiplexer multiplexer_10 (.sel(Q_2), .in_0(progIN[0]), .in_1(1'b0), .out(multiplexer_10_out[0]));
  Multiplexer multiplexer_11 (.sel(Q_4), .in_0(out_9[0]), .in_1(1'b0), .out(multiplexer_11_out[0]));
  RAMDualAccess #(.Bits(13)) pRAM_2 (
    .str(or_3_out), .C(clk), .ld(1'b0), .A1(multiplexer_7_out), .Din1(multiplexer_10_out), .A2(operand[1:0]),
    .D2({pRAM_2_d2, pRAM_operand}));  // open: D1
  RAMDualAccess #(.Bits(13)) rRAM_2 (
    .str(or_4_out), .C(clk), .ld(1'b0), .A1(multiplexer_8_out), .Din1(multiplexer_11_out), .D2(rRAM_operand));  // open: A2, D1
  not not_1 (not_1_out, reset);
  Multiplexer multiplexer_12 (.sel(Q_3), .in_0(P_2), .in_1(1'b0), .out(done));
  Seven_Seg_Hex seven_seg_hex_1 (.d(\output [7:4]), .dp(1'b0));
  Multiplexer #(.Selector_Bits(5)) multiplexer_13 (
    .sel({Q_a, Q_b, Q_c, Q_d, Q_e}), .in_0(start_t), .in_1(1'b0), .in_2(1'b1), .in_3(1'b0), .in_4(1'b0),
    .in_5(Q_d_plus__op), .in_6(1'b1), .in_7(1'b1), .in_8(1'b1), .in_9(1'b1), .in_10(1'b1), .in_11(1'b1),
    .in_12(1'b1), .in_13(1'b1), .in_14(1'b1), .in_15(1'b1), .in_16(1'b1), .in_17(1'b1), .in_18(1'b1),
    .in_19(1'b1), .in_20(1'b1), .in_21(1'b1), .in_22(1'b1), .in_23(1'b1), .in_24(1'b1), .in_25(1'b1),
    .in_26(1'b0), .in_27(1'b0), .in_28(not_1_out), .in_29(1'b0), .in_30(1'b0), .in_31(1'b0),
    .out(multiplexer_13_out));
  Seven_Seg_Hex seven_seg_hex_2 (.d(\output [3:0]), .dp(1'b0));
  D_FF d_ff_5 (.D(multiplexer_13_out), .C(clk), .Q(Q_e));  // open: nQ
  PriorityEncoder #(.Selector_Bits(3)) priorityencoder_1 (
    .in0(Q_6), .in1(Q_8), .in2(Q_11), .in3(Q_14), .in4(Q_15), .in5(Q_25), .in6(1'b0), .in7(1'b0),
    .num(priorityencoder_1_num));  // open: any
  PriorityEncoder priorityencoder_2 (.in0(Q_7), .in1(Q_9), .num(priorityencoder_2_num));  // open: any
  PriorityEncoder #(.Selector_Bits(2)) priorityencoder_3 (
    .in0(Q_10), .in1(Q_12), .in2(Q_13), .in3(1'b0), .num(priorityencoder_3_num));  // open: any
  Multiplexer #(.Selector_Bits(5)) multiplexer_14 (
    .sel({Q_a, Q_b, Q_c, Q_d, Q_e}), .in_0(reset), .in_1(1'b0), .in_2(1'b1), .in_3(1'b0), .in_4(1'b0),
    .in_5(Q_d_plus__op), .in_6(1'b1), .in_7(1'b1), .in_8(1'b1), .in_9(1'b1), .in_10(1'b1), .in_11(1'b1),
    .in_12(1'b1), .in_13(1'b1), .in_14(1'b1), .in_15(1'b1), .in_16(1'b1), .in_17(1'b1), .in_18(1'b1),
    .in_19(1'b1), .in_20(1'b1), .in_21(1'b1), .in_22(1'b1), .in_23(1'b1), .in_24(1'b1), .in_25(1'b1),
    .in_26(1'b0), .in_27(1'b0), .in_28(reset), .in_29(1'b0), .in_30(1'b0), .in_31(1'b0),
    .out(multiplexer_14_out));
  Multiplexer #(.Selector_Bits(3), .Bits(8)) multiplexer_15 (
    .sel(priorityencoder_1_num), .in_0(operand), .in_1(out_10), .in_2(out_11), .in_3(pRAM_operand),
    .in_4(rRAM_operand[7:0]), .in_5(ALU_result_t), .in_6({undriven_2, 1'b0}), .in_7({undriven_2, 1'b0}),
    .out(multiplexer_15_out));
  Multiplexer #(.Bits(8)) multiplexer_16 (
    .sel(priorityencoder_2_num), .in_0(operand), .in_1(out_9), .out(multiplexer_16_out));
  Multiplexer #(.Selector_Bits(2), .Bits(8)) multiplexer_17 (
    .sel(priorityencoder_3_num), .in_0(out_9), .in_1(M), .in_2(M), .in_3({undriven, 1'b0}));  // open: out
  D_FF d_ff_6 (.D(multiplexer_14_out), .C(clk), .Q(Q_e));  // open: nQ
  or or_5 (or_5_out, Q_6, Q_8, Q_11, Q_14, Q_15, Q_25);
  or or_6 (or_6_out, Q_7, Q_9);
  or or_7 (or_7_out, Q_7, Q_9);
  Register register_1 (.D(multiplexer_15_out[0]), .C(clk), .en(or_5_out), .Q(out_9[0]));
  Register register_2 (.D(multiplexer_16_out[0]), .C(clk), .en(or_6_out), .Q(out_10[0]));
  Register register_3 (.D(undriven_3), .C(clk), .en(or_7_out), .Q(out_11[0]));
  or or_8 (or_8_out, start_t, progLoad);
  or or_9 (or_9_out, start_t, progLoad);
  Multiplexer #(.Selector_Bits(5)) multiplexer_18 (
    .sel({Q_a, Q_b, Q_c, Q_d, Q_e}), .in_0(or_8_out), .in_1(progLoad), .in_2(r_cnt_eq_cnt), .in_3(1'b0),
    .in_4(1'b0), .in_5(Q_d_op), .in_6(1'b0), .in_7(1'b0), .in_8(1'b0), .in_9(1'b0), .in_10(1'b0),
    .in_11(1'b0), .in_12(1'b0), .in_13(1'b0), .in_14(1'b0), .in_15(1'b0), .in_16(1'b0), .in_17(1'b1),
    .in_18(eq_t), .in_19(gr), .in_20(le), .in_21(or_9_out), .in_22(1'b0), .in_23(1'b0), .in_24(1'b0),
    .in_25(1'b0), .in_26(1'b1), .in_27(1'b1), .in_28(1'b0), .in_29(1'b0), .in_30(1'b0), .in_31(1'b0),
    .out(multiplexer_18_out));
  assign driver_2_out = Q_27 ? operand[0] : 1'bz;  // Driver driver_2
  or or_10 (or_10_out, Q_2, Q_3);
  or or_11 (or_11_out, Q_0, Q_4);
  Comparator #(.Bits(8)) u_r_cnt_eq_cnt (.a(r_cnt), .b(cnt), .gt(r_cnt_gt_cnt), .eq(r_cnt_eq_cnt), .lt(r_cnt_lt_cnt));
  Comparator #(.Bits(8)) u_r_cnt_eq_16 (.a(r_cnt), .b(8'h10), .gt(r_cnt_gt_16), .eq(r_cnt_eq_16), .lt(r_cnt_lt_16));
  Comparator #(.Bits(8)) u_res_cnt_eq_16 (
    .a(res_cnt), .b(8'h10), .gt(res_cnt_gt_16), .eq(res_cnt_eq_16), .lt(res_cnt_lt_16));
  D_FF d_ff_7 (.D(multiplexer_18_out), .C(clk), .Q(Q_e));  // open: nQ
  CounterPreset counterpreset_1 (
    .en(Q_26), .C(clk), .dir(1'b0), .in(driver_2_out), .ld(Q_27), .clr(Q_0), .out(pc));  // open: ovf
  Counter counter_1 (.en(or_10_out), .C(clk), .clr(or_11_out), .out(r_cnt[0]));  // open: ovf
  Counter counter_2 (.en(progLoad), .C(clk), .clr(Q_3), .out(cnt[0]));  // open: ovf
  Counter counter_3 (.en(P_1), .C(clk), .clr(P_0), .out(res_cnt[0]));  // open: ovf
  Decoder #(.Selector_Bits(2)) decoder_2 (.sel({P_a, P_b}), .out_0(P_0), .out_1(P_1), .out_2(P_2), .out_3(P_3));
  assign driver_3_out = Q_22 ? gt : 1'bz;  // Driver driver_3
  assign driver_4_out = Q_22 ? lt : 1'bz;  // Driver driver_4
  assign driver_5_out = Q_22 ? eq : 1'bz;  // Driver driver_5
  isPrime isprime_1 (.Num(out_9), .Z(isprime_1_z));
  Multiplexer multiplexer_19 (.sel(Q_24), .in_0(driver_5_out), .in_1(isprime_1_z), .out(multiplexer_19_out));
  D_FF u_gr (.D(driver_3_out), .C(clk), .Q(gr));  // open: nQ
  D_FF u_le (.D(driver_4_out), .C(clk), .Q(le));  // open: nQ
  D_FF u_eq (.D(multiplexer_19_out), .C(clk), .Q(le));  // open: nQ
  Comparator #(.Bits(8)) comparator_1 (.a(out_9), .b(out_10), .gt(gt), .eq(eq), .lt(lt));
  ALU alu_1 (.A(out_9), .B(out_10), .op(operand[3:0]), .ans(ALU_result_t));
  // Pins of 1 and 13 bits meet at progIN
  // Pins of 1 and 8 bits meet at r_cnt
  // Pins of 1 and 2 and 5 and 8 bits meet at operand
  // Pins of 1 and 8 bits meet at cnt
  // Pins of 1 and 8 bits meet at out_9
  // Pins of 1 and 8 bits meet at out_10
  // Pins of 1 and 8 bits meet at out_11
  // Pins of 8 and 13 bits meet at \output 
  // Pins of 1 and 2 bits meet at multiplexer_1_out
  // Pins of 1 and 13 bits meet at multiplexer_3_out
  // Pins of 1 and 2 bits meet at driver_1_out
  // Pins of 1 and 2 bits meet at multiplexer_2_out

  // Other names for the same wires on the sheet: accA[7:0] = out_9; accB[7:0] = out_10; ALU_result[7:0] = out_12;
  //   regC[7:0] = out_11

  // Notes on the sheet:
  //   INPUT
  //   RAM
  //   State Q
  //   CHECK
  //   RAM (operand)
  //   OUTPUT
  //   accA
  //   accB
  //   regC
  //   COUNTER
  //   State P
  //   CAL
endmodule

/* Test case:
M N progIN reset progLoad start result clk valid done output
0 0 0 0 0 0 0 0 0 0 0
0 0 0 0 0 0 0 1 0 0 0
0 0 0 1 0 0 0 0 0 0 0
0 0 0 1 0 0 0 1 0 0 0
0 0 0 0 0 0 0 0 0 0 0
0 0 0 0 0 0 0 1 0 0 0
0 0 0 0 0 0 0 0 0 0 0
0 0 0 0 0 0 0 1 0 0 0
0 0 0 0 0 0 0 0 0 0 0
0 0 0 0 0 0 0 1 0 0 0
0 0 0 0 0 0 0 0 0 0 0
0 0 0 0 0 0 0 1 0 0 0
0 0 0 0 0 0 0 0 0 0 0
0 0 0 0 0 0 0 1 0 0 0
0 0 0 0 0 0 0 0 0 0 0
0 0 0 0 0 0 0 1 0 0 0
0 0 0 0 0 0 0 0 0 0 0
0 0 0 0 0 0 0 1 0 0 0
0 0 0 0 0 0 0 0 0 0 0
0 0 0 0 0 0 0 1 0 0 0
0 0 0 0 0 0 0 0 0 0 0
0 0 0 0 0 0 0 1 0 0 0
0 0 0 0 0 0 0 0 0 0 0
0 0 0 0 0 0 0 1 0 0 0
0 0 0 0 0 0 0 0 0 0 0
0 0 0 0 0 0 0 1 0 0 0
0 0 0 0 0 0 0 0 0 0 0
0 0 0 0 0 0 0 1 0 0 0
0 0 0 0 0 0 0 0 0 0 0
0 0 0 0 0 0 0 1 0 0 0
0 0 0 0 0 0 0 0 0 0 0
0 0 0 0 0 0 0 1 0 0 0
0 0 0 0 0 0 0 0 0 0 0
0 0 0 0 0 0 0 1 0 0 0
0 0 0 0 0 0 0 0 0 0 0
0 0 0 0 0 0 0 1 0 0 0
0 0 0 0 0 0 0 0 0 0 0
0 0 0 0 0 0 0 1 0 0 0
0 0 0 0 0 0 0 0 0 0 0
0 0 0 0 0 0 0 1 0 0 0
0 0 0 0 0 0 0 0 0 0 0
0 0 0 0 0 0 0 1 0 0 0
0 0 271 0 1 0 0 0 0 0 0
0 0 0 0 1 0 0 1 0 0 0
0 0 565 0 1 0 0 0 0 0 0
0 0 0 0 1 0 0 1 0 0 0
0 0 4352 0 1 0 0 0 0 0 0
0 0 0 0 1 0 0 1 0 0 0
0 0 2819 0 1 0 0 0 0 0 0
0 0 0 0 1 0 0 1 0 0 0
0 0 7936 0 1 0 0 0 0 0 0
0 0 0 0 1 0 0 1 0 0 0
0 0 0 0 0 1 0 0 0 0 0
0 0 0 0 0 1 0 1 0 0 0
0 0 0 0 0 0 0 0 x 0 0
0 0 0 0 0 0 0 1 x 0 0
0 0 0 0 0 0 0 0 x 0 0
0 0 0 0 0 0 0 1 x 0 0
0 0 0 0 0 0 0 0 x 0 0
0 0 0 0 0 0 0 1 x 0 0
0 0 0 0 0 0 0 0 x 0 0
0 0 0 0 0 0 0 1 x 0 0
0 0 0 0 0 0 0 0 x 0 0
0 0 0 0 0 0 0 1 x 0 0
0 0 0 0 0 0 0 0 x 0 0
0 0 0 0 0 0 0 1 x 0 0
0 0 0 0 0 0 0 0 x 0 0
0 0 0 0 0 0 0 1 x 0 0
0 0 0 0 0 0 0 0 x 0 0
0 0 0 0 0 0 0 1 x 0 0
0 0 0 0 0 0 0 0 x 0 0
0 0 0 0 0 0 0 1 x 0 0
0 0 0 0 0 0 0 0 x 0 0
0 0 0 0 0 0 0 1 x 0 0
0 0 0 0 0 0 0 0 x 0 0
0 0 0 0 0 0 0 1 x 0 0
0 0 0 0 0 0 0 0 x 0 0
0 0 0 0 0 0 0 1 x 0 0
0 0 0 0 0 0 0 0 x 0 0
0 0 0 0 0 0 0 1 x 0 0
0 0 0 0 0 0 0 0 x 0 0
0 0 0 0 0 0 0 1 x 0 0
0 0 0 0 0 0 0 0 x 0 0
0 0 0 0 0 0 0 1 x 0 0
0 0 0 0 0 0 0 0 x 0 0
0 0 0 0 0 0 0 1 x 0 0
0 0 0 0 0 0 0 0 x 0 0
0 0 0 0 0 0 0 1 x 0 0
0 0 0 0 0 0 0 0 x 0 0
0 0 0 0 0 0 0 1 x 0 0
0 0 0 0 0 0 0 0 x 0 0
0 0 0 0 0 0 0 1 x 0 0
0 0 0 0 0 0 0 0 x 0 0
0 0 0 0 0 0 0 1 x 0 0
0 0 0 0 0 0 0 0 x 0 0
0 0 0 0 0 0 0 1 x 0 0
0 0 0 0 0 0 0 0 x 0 0
0 0 0 0 0 0 0 1 x 0 0
0 0 0 0 0 0 0 0 x 0 0
0 0 0 0 0 0 0 1 x 0 0
0 0 0 0 0 0 0 0 x 0 0
0 0 0 0 0 0 0 1 x 0 0
0 0 0 0 0 0 0 0 x 0 0
0 0 0 0 0 0 0 1 x 0 0
0 0 0 0 0 0 0 0 x 0 0
0 0 0 0 0 0 0 1 1 0 0
0 0 0 0 0 0 1 0 1 0 0
0 0 0 0 0 0 1 1 1 0 0
0 0 0 0 0 0 0 0 1 0 0
0 0 0 0 0 0 0 1 1 0 0
0 0 0 0 0 0 0 0 1 0 0
0 0 0 0 0 0 0 1 1 0 0
0 0 0 0 0 0 0 0 1 0 0
0 0 0 0 0 0 0 1 1 0 68
0 0 0 0 0 0 0 0 1 0 68
0 0 0 0 0 0 0 1 1 0 0
0 0 0 0 0 0 0 0 1 0 0
0 0 0 0 0 0 0 1 1 0 0
0 0 0 0 0 0 0 0 1 0 0
0 0 0 0 0 0 0 1 1 0 0
0 0 0 0 0 0 0 0 1 0 0
0 0 0 0 0 0 0 1 1 0 0
0 0 0 0 0 0 0 0 1 0 0
0 0 0 0 0 0 0 1 1 0 0
0 0 0 0 0 0 0 0 1 0 0
0 0 0 0 0 0 0 1 1 0 0
0 0 0 0 0 0 0 0 1 0 0
0 0 0 0 0 0 0 1 1 0 0
0 0 0 0 0 0 0 0 1 0 0
0 0 0 0 0 0 0 1 1 0 0
0 0 0 0 0 0 0 0 1 0 0
0 0 0 0 0 0 0 1 1 0 0
0 0 0 0 0 0 0 0 1 0 0
0 0 0 0 0 0 0 1 1 0 0
0 0 0 0 0 0 0 0 1 0 0
0 0 0 0 0 0 0 1 1 0 0
0 0 0 0 0 0 0 0 1 0 0
0 0 0 0 0 0 0 1 1 0 0
0 0 0 0 0 0 0 0 1 0 0
0 0 0 0 0 0 0 1 1 1 0
0 0 0 0 0 0 0 0 1 1 0
0 0 0 0 0 0 0 1 1 1 0
0 0 0 0 0 0 0 0 1 1 0
*/
