// Digital circuit draft_02.dig as structural Verilog
module draft_02 (
  input  [7:0] M,
  input  [7:0] N,
  input  [12:0] progIN,
  input  start,
  input  reset,
  input  progLoad,
  input  result,
  input  clk,
  output [7:0] out_9,
  output [7:0] out_10,
  output [7:0] out_11,
  output [7:0] out_12,
  output valid,
  output done,
  output [7:0] \output ,
  output [7:0] cnt,
  output [7:0] r_cnt,
  output [7:0] out_18
);

  wire driver_3_out, driver_4_out, driver_5_out, en_A, en_B, en_C, en_rRAM, eq, eq_t, frontbit, gr, gt,
       isprime_1_z, le, lt, multiplexer_5_out, multiplexer_6_out, multiplexer_7_out, multiplexer_10_out,
       multiplexer_13_out, multiplexer_14_out, multiplexer_16_out, multiplexer_17_out, not_1_out, not_2_out,
       not_3_out, not_4_out, or_1_out, or_2_out, or_3_out, or_4_out, or_5_out, or_6_out, or_7_out, or_8_out,
       or_9_out, or_10_out, or_11_out, P_0, P_1, P_2, P_3, P_a, P_a_t, P_b, P_b_t, Q_0, Q_1, Q_2, Q_3, Q_4,
       Q_5, Q_6, Q_7, Q_8, Q_9, Q_10, Q_11, Q_12, Q_13, Q_14, Q_15, Q_16, Q_17, Q_18, Q_a, Q_a_plus_op, Q_b,
       Q_b_plus_op, Q_c, Q_c_plus_op, Q_d, Q_d_plus_op, Q_e, Q_e_plus_op, r_cnt_eq_16, r_cnt_eq_cnt,
       r_cnt_gt_16, r_cnt_gt_cnt, r_cnt_lt_16, r_cnt_lt_cnt, res_cnt_eq_16, res_cnt_gt_16, res_cnt_lt_16,
       result_t, start_t;
  wire [3:0] opcode;
  wire [7:0] driver_1_out, driver_2_out, multiplexer_1_out, multiplexer_2_out, multiplexer_3_out,
       multiplexer_8_out, multiplexer_9_out, multiplexer_12_out, multiplexer_15_out, operand, pRAM_operand,
       res_cnt, rRAM_operand, val;
  wire [12:0] multiplexer_4_out, multiplexer_11_out;
  wire [12:8] pRAM_2_d2;

  Decoder #(.Selector_Bits(5)) decoder_1 (
    .sel({Q_a, Q_b, Q_c, Q_d, Q_e}), .out_0(Q_0), .out_1(Q_1), .out_2(Q_2), .out_3(Q_3), .out_4(Q_4),
    .out_5(Q_5), .out_6(Q_6), .out_7(Q_7), .out_8(Q_8), .out_9(Q_9), .out_10(Q_10), .out_11(Q_11),
    .out_12(Q_12), .out_13(Q_13), .out_14(Q_14), .out_15(Q_15), .out_16(Q_16), .out_17(Q_17), .out_18(Q_18));  // open: out_19, out_20, out_21, out_22, out_23, out_24, out_25, out_26, out_27, out_28, out_29, out_30, out_31
  or or_1 (or_1_out, Q_1, Q_2);
  assign driver_1_out = Q_5 ? out_18 : 8'bz;  // Driver driver_1
  Multiplexer #(.Bits(8)) multiplexer_1 (.sel(Q_2), .in_0(cnt), .in_1(r_cnt), .out(multiplexer_1_out));
  or or_2 (or_2_out, Q_4, en_rRAM);
  Multiplexer #(.Bits(8)) multiplexer_2 (.sel(en_rRAM), .in_0(r_cnt), .in_1(operand), .out(multiplexer_2_out));
  D_FF d_ff_1 (.D(start), .C(clk), .Q(start_t));  // open: nQ
  D_FF d_ff_2 (.D(result), .C(clk), .Q(result_t));  // open: nQ
  Multiplexer #(.Bits(8)) multiplexer_3 (.sel(en_rRAM), .in_0({8{1'b0}}), .in_1(val), .out(multiplexer_3_out));
  Multiplexer #(.Bits(13)) multiplexer_4 (.sel(Q_2), .in_0(progIN), .in_1({13{1'b0}}), .out(multiplexer_4_out));
  not not_1 (not_1_out, reset);
  RAMDualAccess #(.AddrBits(8), .Bits(13)) pRAM (
    .str(or_1_out), .C(clk), .ld(1'b0), .A1(multiplexer_1_out), .Din1(multiplexer_4_out), .A2(driver_1_out),
    .D2({frontbit, opcode, operand}));  // open: D1
  RAMDualAccess #(.AddrBits(8), .Bits(8)) rRAM (
    .str(or_2_out), .C(clk), .ld(1'b0), .A1(multiplexer_2_out), .Din1(multiplexer_3_out), .A2(res_cnt),
    .D2(\output ));  // open: D1
  Multiplexer #(.Selector_Bits(5)) multiplexer_5 (
    .sel({Q_a, Q_b, Q_c, Q_d, Q_e}), .in_0(1'b0), .in_1(1'b0), .in_2(1'b0), .in_3(1'b0), .in_4(1'b0),
    .in_5(Q_a_plus_op), .in_6(1'b1), .in_7(1'b1), .in_8(1'b1), .in_9(1'b1), .in_10(1'b1), .in_11(1'b1),
    .in_12(1'b1), .in_13(1'b1), .in_14(1'b1), .in_15(1'b1), .in_16(1'b0), .in_17(1'b0), .in_18(not_1_out),
    .in_19(1'b0), .in_20(1'b0), .in_21(1'b0), .in_22(1'b0), .in_23(1'b0), .in_24(1'b0), .in_25(1'b0),
    .in_26(1'b0), .in_27(1'b0), .in_28(1'b0), .in_29(1'b0), .in_30(1'b0), .in_31(1'b0),
    .out(multiplexer_5_out));
  Multiplexer multiplexer_6 (.sel(Q_18), .in_0(1'b0), .in_1(1'b1), .out(multiplexer_6_out));
  or or_3 (or_3_out, Q_3, Q_18);
  Multiplexer multiplexer_7 (.sel(P_2), .in_0(1'b0), .in_1(1'b1), .out(multiplexer_7_out));
  or or_4 (or_4_out, Q_3, P_2);
  D_FF d_ff_3 (.D(multiplexer_5_out), .C(clk), .Q(Q_a));  // open: nQ
  Register register_1 (.D(multiplexer_6_out), .C(clk), .en(or_3_out), .Q(valid));
  Register register_2 (.D(multiplexer_7_out), .C(clk), .en(or_4_out), .Q(done));
  or or_5 (or_5_out, Q_1, Q_2);
  Multiplexer #(.Bits(8)) multiplexer_8 (.sel(Q_2), .in_0(cnt), .in_1(r_cnt), .out(multiplexer_8_out));
  or or_6 (or_6_out, Q_4, en_rRAM);
  Multiplexer #(.Bits(8)) multiplexer_9 (.sel(en_rRAM), .in_0(r_cnt), .in_1(operand), .out(multiplexer_9_out));
  Multiplexer #(.Selector_Bits(5)) multiplexer_10 (
    .sel({Q_a, Q_b, Q_c, Q_d, Q_e}), .in_0(1'b0), .in_1(1'b0), .in_2(1'b0), .in_3(1'b0), .in_4(1'b0),
    .in_5(Q_b_plus_op), .in_6(1'b0), .in_7(1'b0), .in_8(1'b0), .in_9(1'b0), .in_10(1'b0), .in_11(1'b0),
    .in_12(1'b0), .in_13(1'b0), .in_14(1'b0), .in_15(1'b0), .in_16(1'b0), .in_17(1'b0), .in_18(1'b0),
    .in_19(1'b0), .in_20(1'b0), .in_21(1'b0), .in_22(1'b0), .in_23(1'b0), .in_24(1'b0), .in_25(1'b0),
    .in_26(1'b0), .in_27(1'b0), .in_28(1'b0), .in_29(1'b0), .in_30(1'b0), .in_31(1'b0),
    .out(multiplexer_10_out));
  D_FF d_ff_4 (.D(multiplexer_10_out), .C(clk), .Q(Q_b));  // open: nQ
  Seven_Seg_Hex seven_seg_hex_1 (.d(\output [7:4]), .dp(1'b0));
  Multiplexer #(.Bits(13)) multiplexer_11 (.sel(Q_2), .in_0(progIN), .in_1({13{1'b0}}), .out(multiplexer_11_out));
  Multiplexer #(.Bits(8)) multiplexer_12 (.sel(en_rRAM), .in_0({8{1'b0}}), .in_1(val), .out(multiplexer_12_out));
  Seven_Seg_Hex seven_seg_hex_2 (.d(\output [3:0]), .dp(1'b0));
  RAMDualAccess #(.AddrBits(8), .Bits(13)) pRAM_2 (
    .str(or_5_out), .C(clk), .ld(1'b0), .A1(multiplexer_8_out), .Din1(multiplexer_11_out), .A2(operand),
    .D2({pRAM_2_d2, pRAM_operand}));  // open: D1
  RAMDualAccess #(.AddrBits(8), .Bits(8)) rRAM_2 (
    .str(or_6_out), .C(clk), .ld(1'b0), .A1(multiplexer_9_out), .Din1(multiplexer_12_out), .A2(operand),
    .D2(rRAM_operand));  // open: D1
  not not_2 (not_2_out, r_cnt_eq_16);
  Multiplexer #(.Selector_Bits(5)) multiplexer_13 (
    .sel({Q_a, Q_b, Q_c, Q_d, Q_e}), .in_0(start_t), .in_1(1'b0), .in_2(1'b0), .in_3(1'b1), .in_4(not_2_out),
    .in_5(Q_c_plus_op), .in_6(1'b0), .in_7(1'b0), .in_8(1'b0), .in_9(1'b0), .in_10(1'b0), .in_11(1'b0),
    .in_12(1'b0), .in_13(1'b0), .in_14(1'b0), .in_15(1'b0), .in_16(1'b1), .in_17(1'b1), .in_18(1'b0),
    .in_19(1'b0), .in_20(1'b0), .in_21(1'b0), .in_22(1'b0), .in_23(1'b0), .in_24(1'b0), .in_25(1'b0),
    .in_26(1'b0), .in_27(1'b0), .in_28(1'b0), .in_29(1'b0), .in_30(1'b0), .in_31(1'b0),
    .out(multiplexer_13_out));
  D_FF d_ff_5 (.D(multiplexer_13_out), .C(clk), .Q(Q_c));  // open: nQ
  Comparator #(.Bits(8)) u_r_cnt_eq_cnt (.a(r_cnt), .b(cnt), .gt(r_cnt_gt_cnt), .eq(r_cnt_eq_cnt), .lt(r_cnt_lt_cnt));
  Comparator #(.Bits(8)) u_r_cnt_eq_16 (.a(r_cnt), .b(8'h10), .gt(r_cnt_gt_16), .eq(r_cnt_eq_16), .lt(r_cnt_lt_16));
  Comparator #(.Bits(8)) u_res_cnt_eq_16 (
    .a(res_cnt), .b(8'h10), .gt(res_cnt_gt_16), .eq(res_cnt_eq_16), .lt(res_cnt_lt_16));
  Counter #(.Bits(8)) counter_1 (.en(P_1), .C(clk), .clr(P_0), .out(res_cnt));  // open: ovf
  Multiplexer #(.Selector_Bits(5)) multiplexer_14 (
    .sel({Q_a, Q_b, Q_c, Q_d, Q_e}), .in_0(reset), .in_1(1'b0), .in_2(1'b1), .in_3(1'b0), .in_4(1'b0),
    .in_5(Q_d_plus_op), .in_6(1'b0), .in_7(1'b0), .in_8(1'b0), .in_9(1'b0), .in_10(1'b0), .in_11(1'b0),
    .in_12(1'b0), .in_13(1'b0), .in_14(1'b0), .in_15(1'b0), .in_16(1'b0), .in_17(1'b0), .in_18(1'b1),
    .in_19(1'b0), .in_20(1'b0), .in_21(1'b0), .in_22(1'b0), .in_23(1'b0), .in_24(1'b0), .in_25(1'b0),
    .in_26(1'b0), .in_27(1'b0), .in_28(1'b0), .in_29(1'b0), .in_30(1'b0), .in_31(1'b0),
    .out(multiplexer_14_out));
  Register #(.Bits(8)) register_3 (.D(val), .C(clk), .en(en_B), .Q(out_10));
  D_FF d_ff_6 (.D(multiplexer_14_out), .C(clk), .Q(Q_d));  // open: nQ
  Multiplexer #(.Bits(8)) multiplexer_15 (.sel(frontbit), .in_0(val), .in_1(out_12), .out(multiplexer_15_out));
  or or_7 (or_7_out, en_A, Q_15);
  or or_8 (or_8_out, Q_2, Q_3);
  or or_9 (or_9_out, Q_0, Q_4);
  Register #(.Bits(8)) register_4 (.D(multiplexer_15_out), .C(clk), .en(or_7_out), .Q(out_9));
  Register #(.Bits(8)) register_5 (.D(val), .C(clk), .en(en_C), .Q(out_11));
  assign driver_2_out = Q_17 ? operand : 8'bz;  // Driver driver_2
  or or_10 (or_10_out, start_t, progLoad);
  or or_11 (or_11_out, eq_t, gr);
  CounterPreset #(.Bits(8), .maxValue(256)) counterpreset_1 (
    .en(Q_16), .C(clk), .dir(1'b0), .in(driver_2_out), .ld(Q_17), .clr(Q_0), .out(out_18));  // open: ovf
  Counter #(.Bits(8)) counter_2 (.en(or_8_out), .C(clk), .clr(or_9_out), .out(r_cnt));  // open: ovf
  Counter #(.Bits(8)) counter_3 (.en(progLoad), .C(clk), .clr(Q_3), .out(cnt));  // open: ovf
  Multiplexer #(.Selector_Bits(5)) multiplexer_16 (
    .sel({Q_a, Q_b, Q_c, Q_d, Q_e}), .in_0(or_10_out), .in_1(progLoad), .in_2(r_cnt_eq_cnt), .in_3(1'b0),
    .in_4(1'b0), .in_5(Q_e_plus_op), .in_6(1'b0), .in_7(1'b1), .in_8(eq_t), .in_9(gr), .in_10(le),
    .in_11(or_11_out), .in_12(1'b0), .in_13(1'b0), .in_14(1'b0), .in_15(1'b0), .in_16(1'b1), .in_17(1'b1),
    .in_18(1'b0), .in_19(1'b0), .in_20(1'b0), .in_21(1'b0), .in_22(1'b0), .in_23(1'b0), .in_24(1'b0),
    .in_25(1'b0), .in_26(1'b0), .in_27(1'b0), .in_28(1'b0), .in_29(1'b0), .in_30(1'b0), .in_31(1'b0),
    .out(multiplexer_16_out));
  D_FF d_ff_7 (.D(multiplexer_16_out), .C(clk), .Q(Q_e));  // open: nQ
  assign driver_3_out = Q_12 ? gt : 1'bz;  // Driver driver_3
  assign driver_4_out = Q_12 ? lt : 1'bz;  // Driver driver_4
  assign driver_5_out = Q_12 ? eq : 1'bz;  // Driver driver_5
  isPrime isprime_1 (.Num(out_9), .Z(isprime_1_z));
  Multiplexer multiplexer_17 (.sel(Q_14), .in_0(driver_5_out), .in_1(isprime_1_z), .out(multiplexer_17_out));
  // MOVE move_1: pin names not known; wires that end beside it: {frontbit, opcode}, operand, out_9, out_10, out_11, rRAM_operand, pRAM_operand, M, N, val, en_A, en_B, en_C, en_rRAM
  Decoder #(.Selector_Bits(2)) decoder_2 (.sel({P_a_t, P_b_t}), .out_0(P_0), .out_1(P_1), .out_2(P_2), .out_3(P_3));
  not not_3 (not_3_out, reset);
  not not_4 (not_4_out, reset);
  LookUpTable lookuptable_1 (
    .in0(opcode[0]), .in1(opcode[1]), .in2(opcode[2]), .in3(opcode[3]), .in4(frontbit), .out(Q_a_plus_op));
  LookUpTable lookuptable_2 (
    .in0(opcode[0]), .in1(opcode[1]), .in2(opcode[2]), .in3(opcode[3]), .in4(frontbit), .out(Q_b_plus_op));
  LookUpTable lookuptable_3 (
    .in0(opcode[0]), .in1(opcode[1]), .in2(opcode[2]), .in3(opcode[3]), .in4(frontbit), .out(Q_c_plus_op));
  LookUpTable lookuptable_4 (
    .in0(opcode[0]), .in1(opcode[1]), .in2(opcode[2]), .in3(opcode[3]), .in4(frontbit), .out(Q_d_plus_op));
  LookUpTable lookuptable_5 (
    .in0(opcode[0]), .in1(opcode[1]), .in2(opcode[2]), .in3(opcode[3]), .in4(frontbit), .out(Q_e_plus_op));
  D_FF u_gr (.D(driver_3_out), .C(clk), .Q(gr));  // open: nQ
  D_FF u_le (.D(driver_4_out), .C(clk), .Q(le));  // open: nQ
  D_FF u_eq (.D(multiplexer_17_out), .C(clk), .Q(eq_t));  // open: nQ
  Comparator #(.Bits(8)) comparator_1 (.a(out_9), .b(out_10), .gt(gt), .eq(eq), .lt(lt));
  ALU alu_1 (.A(out_9), .B(out_10), .op(opcode), .ans(out_12));
  Multiplexer #(.Selector_Bits(2)) multiplexer_18 (
    .sel({P_b_t, P_a_t}), .in_0(1'b0), .in_1(res_cnt_eq_16), .in_2(not_3_out), .in_3(1'b0), .out(P_a));
  Multiplexer #(.Selector_Bits(2)) multiplexer_19 (
    .sel({P_b_t, P_a_t}), .in_0(1'b0), .in_1(res_cnt_eq_16), .in_2(not_4_out), .in_3(1'b0), .out(P_b));
  D_FF d_ff_8 (.D(P_a), .C(clk), .Q(P_a_t));  // open: nQ
  D_FF d_ff_9 (.D(P_b), .C(clk), .Q(P_b_t));  // open: nQ

  // Other names for the same wires on the sheet: opcode[4] = frontbit; accA[7:0] = out_9; accB[7:0] = out_10;
  //   ALU_result[7:0] = out_12; pc[7:0] = out_18; regC[7:0] = out_11

  // Notes on the sheet:
  //   INPUT
  //   RAM
  //   StateQ
  //   OUTPUT
  //   RAM (operand)
  //   CHECK
  //   COUNTER
  //   Reg
  //   CAL
  //   StateP
  //   contents of lookuptable_1 (hex, n*v repeats v):
  //   1,30*0,1
  //   contents of lookuptable_2 (hex, n*v repeats v):
  //   13*0,18*1
  //   contents of lookuptable_3 (hex, n*v repeats v):
  //   0,12*1,4*0,14*1
  //   contents of lookuptable_4 (hex, n*v repeats v):
  //   0,12*1,0,0,8*1,0,6*1,0,1
  //   contents of lookuptable_5 (hex, n*v repeats v):
  //   12*0,1,0,1,0,7*1,0,5*1,0,1
endmodule
