// Digital circuit draft_03.dig as structural Verilog
module draft_03 (
  input  [7:0] M,
  input  [7:0] N,
  input  [12:0] progIN,
  input  start,
  input  reset,
  input  progLoad,
  input  result,
  input  clk,
  output valid,
  output done,
  output [7:0] \output 
);

  wire _00000, _00001, _00010, _00011, _00100, _00101, _00110, _00111, _01000, _01001, _01010, _01011,
       _01100, _01101, _01110, _01111, _10000, _10001, _10010, _10011, _10100, _10101, _10110, _10111,
       _11000, _11001, _11010, _11011, _11100, _11101, _11110, _11111, and_3_out, and_4_out, and_5_out,
       and_6_out, and_7_out, and_8_out, d_ff_1_nq, d_ff_2_q, d_ff_3_q, enA, enB, enC, eq, eq_t, gr, gt, jump,
       le, lt, multiplexer_8_out, multiplexer_9_out, multiplexer_10_out, multiplexer_11_out,
       multiplexer_12_out, multiplexer_13_out, multiplexer_14_out, multiplexer_15_out, multiplexer_16_out,
       not_2_out, not_3_out, not_4_out, not_5_out, or_1_out, or_2_out, or_3_out, or_4_out, or_7_out,
       or_11_out, or_12_out, or_13_out, or_14_out, or_15_out, or_16_out, P_0, P_1, P_2, P_3, P_a, P_b, Q_0,
       Q_1, Q_2, Q_3, Q_4, Q_5, Q_6, Q_7, Q_a, Q_b, Q_c, r_cnt__eq__16, r_cnt_eq_16, r_cnt_gt_16,
       r_cnt_lt_16, res_cnt_eq_16, res_cnt_gt_16, res_cnt_lt_16, result_cnt_eq_16, rom_1_d, start_t;
  wire [4:0] bitcount_1_out, opcode;
  wire [7:0] A, A_B, A_lt__lt_B, accA, accB, AND, cnt, DIFF, DIV, MOD, MUL, multiplexer_1_out,
       multiplexer_2_out, multiplexer_3_out, multiplexer_4_out, multiplexer_5_out, multiplexer_6_out,
       operand, OR, pc, pRAM_operand, r_cnt, regC, res_cnt, rRAM_operand, SUM, val, XOR;
  wire [12:8] pRAM_d1;

  or or_1 (or_1_out, P_0, result);
  Multiplexer #(.Bits(8)) multiplexer_1 (.sel(_01001), .in_0(cnt), .in_1(operand), .out(multiplexer_1_out));
  D_FF d_ff_1 (.D(start), .C(clk), .nQ(d_ff_1_nq));  // open: Q
  Counter #(.Bits(8)) u_cnt (.en(progLoad), .C(clk), .clr(P_2), .out(cnt));  // open: ovf
  Counter #(.Bits(8)) u_r_cnt (.en(Q_3), .C(clk), .clr(r_cnt_eq_16), .out(r_cnt));  // open: ovf
  Counter #(.Bits(8)) result_cnt (.en(P_1), .C(clk), .clr(or_1_out), .out(res_cnt));  // open: ovf
  RAMDualAccess #(.AddrBits(8), .Bits(13)) pRAM (
    .str(progLoad), .C(clk), .ld(_01001), .A1(multiplexer_1_out), .Din1(progIN), .A2(pc),
    .D1({pRAM_d1, pRAM_operand}), .D2({opcode, operand}));
  D_FF d_ff_2 (.D(start), .C(clk), .Q(d_ff_2_q));  // open: nQ
  D_FF d_ff_3 (.D(d_ff_1_nq), .C(clk), .Q(d_ff_3_q));  // open: nQ
  and and_1 (start_t, d_ff_2_q, d_ff_3_q);
  or or_2 (or_2_out, start, reset, _11111);
  Comparator #(.Bits(8)) u_r_cnt_eq_16 (.a(r_cnt), .b(8'h10), .gt(r_cnt_gt_16), .eq(r_cnt_eq_16), .lt(r_cnt_lt_16));
  Comparator #(.Bits(8)) res_cnt__eq__16 (
    .a(res_cnt), .b(8'h10), .gt(res_cnt_gt_16), .eq(res_cnt_eq_16), .lt(res_cnt_lt_16));
  CounterPreset #(.maxValue(256), .Bits(8)) u_pc (
    .en(Q_4), .C(clk), .dir(1'b0), .in(operand), .ld(jump), .clr(or_2_out), .out(pc));  // open: ovf
  or or_3 (or_3_out, _01011, Q_3);
  Multiplexer #(.Selector_Bits(2), .Bits(8)) multiplexer_2 (
    .sel({_01011, _01010}), .in_0(r_cnt), .in_1(operand), .in_2(operand), .in_3({8{1'b0}}),
    .out(multiplexer_2_out));
  Multiplexer #(.Bits(8)) multiplexer_3 (.sel(_01011), .in_0({8{1'b0}}), .in_1(val), .out(multiplexer_3_out));
  or or_4 (or_4_out, start, reset);
  Multiplexer #(.Bits(8)) multiplexer_4 (.sel(reset), .in_0(val), .in_1({8{1'b0}}), .out(multiplexer_4_out));
  Multiplexer #(.Bits(8)) multiplexer_5 (.sel(reset), .in_0(val), .in_1({8{1'b0}}), .out(multiplexer_5_out));
  Multiplexer #(.Bits(8)) multiplexer_6 (.sel(reset), .in_0(val), .in_1({8{1'b0}}), .out(multiplexer_6_out));
  or or_5 (done, res_cnt_eq_16, P_2);
  RAMDualAccess #(.AddrBits(8), .Bits(8)) rRAM (
    .str(or_3_out), .C(clk), .ld(_01010), .A1(multiplexer_2_out), .Din1(multiplexer_3_out), .A2(res_cnt),
    .D1(rRAM_operand), .D2(\output ));
  RS_FF_AS rs_ff_as_1 (.S(Q_5), .R(or_4_out), .Q(valid));  // open: nQ
  Seven_Seg_Hex seven_seg_hex_1 (.d(\output [7:4]), .dp(1'b0));
  Register #(.Bits(8)) u_accA (.D(multiplexer_4_out), .C(clk), .en(enA), .Q(accA));
  Register #(.Bits(8)) u_accB (.D(multiplexer_5_out), .C(clk), .en(enB), .Q(accB));
  Register #(.Bits(8)) u_regC (.D(multiplexer_6_out), .C(clk), .en(enC), .Q(regC));
  Seven_Seg_Hex seven_seg_hex_2 (.d(\output [3:0]), .dp(1'b0));
  assign AND = accA & accB;  // And and_2, 8 bits wide
  assign OR = accA | accB;  // Or or_6, 8 bits wide
  assign XOR = accA ^ accB;  // XOr xor_1, 8 bits wide
  Add #(.Bits(8)) add_1 (.a(accA), .b(accB), .c_i(1'b0), .s(SUM));  // open: c_o
  Sub #(.Bits(8)) sub_1 (.a(accA), .b(accB), .c_i(1'b0), .s(DIFF));  // open: c_o
  Mul #(.Bits(4)) mul_1 (.a(accA[3:0]), .b(accB[3:0]), .mul(MUL));
  Div #(.Bits(8)) div_1 (.a(accA), .b(accB), .q(DIV), .r(MOD));
  assign A = ~accA;  // Not not_1, 8 bits wide
  BarrelShifter #(.Bits(8), .barrelShifterMode("arithmetic")) barrelshifter_1 (
    .in(accA), .shift({1'b0, accB[2:0]}), .out(A_lt__lt_B));
  LookUpTable #(.Bits(8)) exponent (
    .in0(accB[0]), .in1(accB[1]), .in2(accB[2]), .in3(accA[0]), .in4(accA[1]), .in5(accA[2]), .out(A_B));
  Demultiplexer #(.Selector_Bits(5)) demultiplexer_1 (
    .sel(opcode), .in(Q_4), .out_0(_00000), .out_1(_00001), .out_2(_00010), .out_3(_00011), .out_4(_00100),
    .out_5(_00101), .out_6(_00110), .out_7(_00111), .out_8(_01000), .out_9(_01001), .out_10(_01010),
    .out_11(_01011), .out_12(_01100), .out_13(_01101), .out_14(_01110), .out_15(_01111), .out_16(_10000),
    .out_17(_10001), .out_18(_10010), .out_19(_10011), .out_20(_10100), .out_21(_10101), .out_22(_10110),
    .out_23(_10111), .out_24(_11000), .out_25(_11001), .out_26(_11010), .out_27(_11011), .out_28(_11100),
    .out_29(_11101), .out_30(_11110), .out_31(_11111));
  Decoder #(.Selector_Bits(3)) decoder_1 (
    .sel({Q_a, Q_b, Q_c}), .out_0(Q_0), .out_1(Q_1), .out_2(Q_2), .out_3(Q_3), .out_4(Q_4), .out_5(Q_5),
    .out_6(Q_6), .out_7(Q_7));
  Decoder #(.Selector_Bits(2)) decoder_2 (.sel({P_a, P_b}), .out_0(P_0), .out_1(P_1), .out_2(P_2), .out_3(P_3));
  not not_2 (not_2_out, reset);
  Multiplexer #(.Selector_Bits(5), .Bits(8)) multiplexer_7 (
    .sel(opcode), .in_0({8{1'b0}}), .in_1(operand), .in_2(operand), .in_3(accB), .in_4(accA), .in_5(accA),
    .in_6(regC), .in_7(M), .in_8(N), .in_9(pRAM_operand), .in_10(rRAM_operand), .in_11(accA),
    .in_12({8{1'b0}}), .in_13({8{1'b0}}), .in_14({8{1'b0}}), .in_15({8{1'b0}}), .in_16({8{1'b0}}),
    .in_17(SUM), .in_18(DIFF), .in_19(MUL), .in_20(DIV), .in_21(MOD), .in_22(A_B), .in_23({8{1'b0}}),
    .in_24(A), .in_25(AND), .in_26(OR), .in_27(XOR), .in_28(A_lt__lt_B), .in_29({8{1'b0}}),
    .in_30({8{1'b0}}), .in_31({8{1'b0}}), .out(val));
  Multiplexer #(.Selector_Bits(3)) multiplexer_8 (
    .sel({Q_a, Q_b, Q_c}), .in_0(start_t), .in_1(1'b0), .in_2(1'b0), .in_3(1'b0), .in_4(1'b1),
    .in_5(not_2_out), .in_6(1'b0), .in_7(1'b0), .out(multiplexer_8_out));
  or or_7 (or_7_out, start, progLoad, reset);
  and and_3 (and_3_out, ~reset, ~result);  // And
  D_FF d_ff_4 (.D(multiplexer_8_out), .C(clk), .Q(Q_a));  // open: nQ
  Multiplexer #(.Selector_Bits(2)) multiplexer_9 (
    .sel({P_a, P_b}), .in_0(1'b0), .in_1(result_cnt_eq_16), .in_2(and_3_out), .in_3(1'b0),
    .out(multiplexer_9_out));
  and and_4 (and_4_out, ~or_7_out, multiplexer_9_out);  // And
  BitCount #(.Bits(16)) bitcount_1 (
    .in({_11100, _11011, _11010, _11001, _11000, _10110, _10101, _10100, _10011, _10010, _10001, _01010, _01001, _00110, _00011, _00001}),
    .out(bitcount_1_out));
  not not_3 (not_3_out, r_cnt__eq__16);
  D_FF d_ff_5 (.D(and_4_out), .C(clk), .Q(P_a));  // open: nQ
  or or_8 (enA, bitcount_1_out[0], reset);
  or or_9 (enB, reset, _00010, _00100);
  or or_10 (enC, reset, _00101, _00111, _01000);
  Multiplexer #(.Selector_Bits(3)) multiplexer_10 (
    .sel({Q_a, Q_b, Q_c}), .in_0(reset), .in_1(1'b0), .in_2(1'b1), .in_3(not_3_out), .in_4(1'b0),
    .in_5(reset), .in_6(1'b0), .in_7(1'b0), .out(multiplexer_10_out));
  D_FF d_ff_6 (.D(multiplexer_10_out), .C(clk), .Q(Q_a));  // open: nQ
  or or_11 (or_11_out, start, progLoad, reset);
  not not_4 (not_4_out, result_cnt_eq_16);
  ROM #(.AddrBits(8)) rom_1 (.A(accA), .sel(1'b1), .D(rom_1_d));
  Multiplexer multiplexer_11 (.sel(_10111), .in_0(1'b0), .in_1(gt), .out(multiplexer_11_out));
  or or_12 (or_12_out, start, _10111);
  and and_5 (and_5_out, ~start_t, ~reset);  // And
  Multiplexer #(.Selector_Bits(2)) multiplexer_12 (
    .sel({P_a, P_b}), .in_0(result), .in_1(not_4_out), .in_2(result), .in_3(1'b0), .out(multiplexer_12_out));
  and and_6 (and_6_out, eq, _10111);
  and and_7 (and_7_out, _11101, rom_1_d);
  or or_13 (or_13_out, start, _10111, _11101);
  not not_5 (not_5_out, r_cnt_eq_16);
  and and_8 (and_8_out, ~or_11_out, multiplexer_12_out);  // And
  Register register_1 (.D(multiplexer_11_out), .C(clk), .en(or_12_out), .Q(gr));
  Multiplexer #(.Selector_Bits(3)) multiplexer_13 (
    .sel({Q_a, Q_b, Q_c}), .in_0(progLoad), .in_1(progLoad), .in_2(1'b1), .in_3(not_5_out), .in_4(_11111),
    .in_5(and_5_out), .in_6(1'b0), .in_7(1'b0), .out(multiplexer_13_out));
  or or_14 (or_14_out, and_6_out, and_7_out);
  D_FF d_ff_7 (.D(multiplexer_13_out), .C(clk), .Q(Q_c));  // open: nQ
  D_FF d_ff_8 (.D(and_8_out), .C(clk), .Q(P_a));  // open: nQ
  Multiplexer multiplexer_14 (.sel(start), .in_0(or_14_out), .in_1(1'b0), .out(multiplexer_14_out));
  Multiplexer multiplexer_15 (.sel(_10111), .in_0(1'b0), .in_1(gt), .out(multiplexer_15_out));
  or or_15 (or_15_out, start, _10111);
  Register register_2 (.D(multiplexer_14_out), .C(clk), .en(or_13_out), .Q(eq_t));
  Register register_3 (.D(multiplexer_15_out), .C(clk), .en(or_15_out), .Q(gr));
  Comparator #(.Signed("true"), .Bits(8)) comparator_1 (.a(accA), .b(accB), .gt(gt), .eq(eq), .lt(lt));
  Multiplexer multiplexer_16 (.sel(_10111), .in_0(1'b0), .in_1(lt), .out(multiplexer_16_out));
  or or_16 (or_16_out, start, _10111);
  Register register_4 (.D(multiplexer_16_out), .C(clk), .en(or_16_out), .Q(le));

  // Other names for the same wires on the sheet: en_rRAM = _01011

  // Notes on the sheet:
  //   INPUT
  //   Counter
  //   RAM
  //   OUTPUT
  //   contents of exponent (hex, n*v repeats v):
  //   1,0,a0000,a00000,0,40000,0,0,9*1,2,4,8,10,20,40,80,1,3,9,1b,51
  //   ,f3,d9,8b,1,4,10,40,4*0,1,5,19,7d,71,35,9,2d,1,6,24,d8,10,60,40
  //   ,80,1,7,31,57,61,a7,91,f7,0,0,0,1,0,0,0,1,0,1,5*0,1,0,0,0,1,5*0
  //   ,1,7*0,1,0,0,0,1,0,1,0,0,0,1,0,1,0,0,0,1,13*0,1,0,0,0,1,5*0,1
  //   ,0,1,9*0,1,0,1,5*0,1,5*0,1,0,0,0,1,5*0,1,5*0,1,0,1,9*0,1,0,1,0,0,0
  //   ,1,0,1,11*0,1,11*0,1,0,0,0,1,0,1,0,0,0,1,5*0,1,0,1,9*0,1
  //   Opcode
  //   StateQ
  //   isPrime
  //   contents of rom_1 (hex, n*v repeats v):
  //   0,0,1,1,0,1,0,1,0,0,0,1,0,1,0,0,0,1,0,1,0,0,0,1,5*0,1,0,1,5*0
  //   ,1,0,0,0,1,0,1,0,0,0,1,5*0,1,5*0,1,0,1,5*0,1,0,0,0,1,0,1,5*0,1
  //   ,0,0,0,1,5*0,1,7*0,1,0,0,0,1,0,1,0,0,0,1,0,1,0,0,0,1,13*0,1,0,0,0
  //   ,1,5*0,1,0,1,9*0,1,0,1,5*0,1,5*0,1,0,0,0,1,5*0,1,5*0,1,0,1,9*0
  //   ,1,0,1,0,0,0,1,0,1,11*0,1,11*0,1,0,0,0,1,0,1,0,0,0,1,5*0,1,0,1
  //   ,9*0,1
endmodule
