// Digital circuit 04.dig as structural Verilog
module _04 (
  input  [6:0] In,
  output [6:0] Output
);

  wire C1, C2, C3;
  wire [6:0] demultiplexer_1_out_7;

  xor xor_1 (C1, In[3], In[2], In[1], In[0]);
  xor xor_2 (C2, In[5], In[4], In[1], In[0]);
  xor xor_3 (C3, In[6], In[4], In[2], In[0]);
  Demultiplexer #(.Selector_Bits(3)) demultiplexer_1 (
    .sel({C1, C2, C3}), .in(1'b1), .out_1(demultiplexer_1_out_7[6]), .out_2(demultiplexer_1_out_7[5]),
    .out_3(demultiplexer_1_out_7[4]), .out_4(demultiplexer_1_out_7[3]), .out_5(demultiplexer_1_out_7[2]),
    .out_6(demultiplexer_1_out_7[1]), .out_7(demultiplexer_1_out_7[0]));  // open: out_0
  assign Output = In ^ demultiplexer_1_out_7;  // XOr xor_4, 7 bits wide
endmodule
