// Digital circuit Template.dig as structural Verilog
module Template (
  input  D,
  input  Clear,
  input  Clock,
  output Q,
  output Q_2
);

  wire nand_1_out, nand_2_out, nand_3_out, nand_4_out, or_1_out;

  nand nand_1 (nand_1_out, or_1_out, nand_2_out);
  nand nand_2 (nand_2_out, nand_1_out, Clock);
  nand nand_3 (nand_3_out, nand_2_out, Clock, or_1_out);
  nand nand_4 (nand_4_out, nand_3_out, D);
  or or_1 (or_1_out, nand_4_out, Clear);
  nand nand_5 (Q, nand_2_out, Q_2);
  nand nand_6 (Q_2, Q, nand_3_out);

  // Notes on the sheet:
  //   D Flip-Flop
endmodule
