// Digital circuit gcd_template.dig as structural Verilog
module gcd_template (
  input  [7:0] A,
  input  [7:0] B,
  input  start,
  input  clear,
  input  clk,
  output busy,
  output [7:0] \output 
);

  wire a_eq_b, a_gt_b, and_1_out, and_2_out, and_3_out, multiplexer_3_out, multiplexer_4_out, not_2_out,
       or_1_out, or_2_out, S0, S1, S2, S3, Sa, Sb;
  wire [7:0] a_t, b_t, multiplexer_1_out, multiplexer_2_out, sub_1_s, sub_2_s;

  Sub #(.Bits(8)) sub_1 (.a(a_t), .b(b_t), .c_i(1'b0), .s(sub_1_s));  // open: c_o
  or or_1 (or_1_out, S0, S2);
  Sub #(.Bits(8)) sub_2 (.a(b_t), .b(a_t), .c_i(1'b0), .s(sub_2_s));  // open: c_o
  or or_2 (or_2_out, S0, S3);
  Multiplexer #(.Bits(8)) multiplexer_1 (.sel(S2), .in_0(A), .in_1(sub_1_s), .out(multiplexer_1_out));
  Multiplexer #(.Bits(8)) multiplexer_2 (.sel(S3), .in_0(B), .in_1(sub_2_s), .out(multiplexer_2_out));
  Decoder #(.Selector_Bits(2)) decoder_1 (.sel({Sb, Sa}), .out_0(S0), .out_1(S1), .out_2(S2), .out_3(S3));
  Register #(.Bits(8)) Reg_a (.D(multiplexer_1_out), .C(clk), .en(or_1_out), .Q(a_t));
  Register #(.Bits(8)) Reg_b (.D(multiplexer_2_out), .C(clk), .en(or_2_out), .Q(b_t));
  not not_1 (busy, S0);
  Comparator #(.Bits(8)) comp (.a(a_t), .b(b_t), .gt(a_gt_b), .eq(a_eq_b));  // open: lt
  Register #(.Bits(8)) Reg_out (.D(a_t), .C(clk), .en(S1), .Q(\output ));
  not not_2 (not_2_out, a_eq_b);
  and and_1 (and_1_out, ~a_eq_b, ~a_gt_b);  // And
  Multiplexer #(.Selector_Bits(2)) multiplexer_3 (
    .sel({Sb, Sa}), .in_0(1'b0), .in_1(not_2_out), .in_2(1'b0), .in_3(1'b0), .out(multiplexer_3_out));
  Multiplexer #(.Selector_Bits(2)) multiplexer_4 (
    .sel({Sb, Sa}), .in_0(start), .in_1(and_1_out), .in_2(1'b1), .in_3(1'b1), .out(multiplexer_4_out));
  and and_2 (and_2_out, multiplexer_3_out, ~clear);  // And
  and and_3 (and_3_out, multiplexer_4_out, ~clear);  // And
  Seven_Seg_Hex seven_seg_hex_1 (.d(\output [7:4]), .dp(1'b0));
  Seven_Seg_Hex seven_seg_hex_2 (.d(\output [3:0]), .dp(1'b0));
  D_FF d_ff_1 (.D(and_2_out), .C(clk), .Q(Sb));  // open: nQ
  D_FF d_ff_2 (.D(and_3_out), .C(clk), .Q(Sa));  // open: nQ

  // Other names for the same wires on the sheet: out[7:0] = \output 
endmodule

/* Test case:
A B start clear clk busy output
0xF 0x6 0 0 0 0 0
0xF 0x6 0 0 1 X 0
0xF 0x6 1 0 0 X 0
0xF 0x6 1 0 1 X 0
0xF 0x6 1 0 0 X 0
loop(x,1000)
0xF 0x6 0 0 1 X X
0xF 0x6 0 0 0 X X
end loop
0xF 0x6 0 0 0 0 0x3
*/
