// Digital circuit template.dig as structural Verilog
module template (
  input  reset,
  input  clk,
  output A,
  output B,
  output C
);

  wire and_1_out, and_2_out, and_3_out, and_4_out, next_A, next_B, not_1_out, not_2_out, not_3_out;

  and and_1 (and_1_out, next_A, ~reset);  // And
  and and_2 (and_2_out, next_B, ~reset);  // And
  and and_3 (and_3_out, A, ~reset);  // And
  D_FF d_ff_1 (.D(and_1_out), .C(clk), .Q(A));  // open: nQ
  D_FF d_ff_2 (.D(and_2_out), .C(clk), .Q(B));  // open: nQ
  D_FF d_ff_3 (.D(and_3_out), .C(clk), .Q(C));  // open: nQ
  not not_1 (not_1_out, C);
  not not_2 (not_2_out, B);
  not not_3 (not_3_out, A);
  and and_4 (and_4_out, not_3_out, not_1_out);
  and and_5 (next_A, B, not_1_out);
  or or_1 (next_B, and_4_out, not_2_out);

  // Other names for the same wires on the sheet: next_C = A
endmodule

/* Test case:
clk reset C B A
0 0 0 0 0 
0 1 0 0 0
1 1 0 0 0
0 0 0 0 0
1 0 0 1 0
0 0 0 1 0
1 0 0 1 1
0 0 0 1 1
1 0 1 0 1
0 0 1 0 1
1 0 1 1 0
0 0 1 1 0
1 0 0 0 0
0 0 0 0 0
1 0 0 1 0
0 0 0 1 0
1 0 0 1 1
0 0 0 1 1
1 0 1 0 1
0 0 1 0 1
1 0 1 1 0
0 0 1 1 0
1 0 0 0 0
0 0 0 0 0
*/
