// Digital circuit Template.dig as structural Verilog
module Template (
  input  [2:0] in0,
  input  [2:0] in1,
  input  addsubtract,
  output [2:0] out
);

  wire and_1_out, and_2_out, and_3_out, and_4_out, and_5_out, and_6_out, and_7_out, and_8_out, and_9_out,
       and_10_out, and_11_out, and_12_out, and_13_out, and_14_out, and_15_out, and_16_out, and_17_out,
       and_18_out, and_19_out, and_20_out, and_21_out, and_22_out, and_23_out, and_24_out, and_25_out,
       and_26_out, and_27_out, and_28_out, and_29_out, not_1_out, not_2_out, not_3_out, not_4_out, not_5_out,
       not_6_out, not_7_out, not_8_out, not_9_out, not_10_out, not_11_out, not_12_out, not_13_out,
       not_14_out, numone0_0, numone0_1, numone1_0, numone1_1;
  wire [1:0] subtract;
  wire [2:0] add;

  not not_1 (not_1_out, in1[2]);
  not not_2 (not_2_out, numone0_1);
  not not_3 (not_3_out, in1[1]);
  not not_4 (not_4_out, numone0_0);
  not not_5 (not_5_out, in1[0]);
  and and_1 (and_1_out, not_1_out, not_3_out, in1[0]);
  and and_2 (and_2_out, not_1_out, in1[1], not_5_out);
  and and_3 (and_3_out, in1[2], not_3_out, not_5_out);
  and and_4 (and_4_out, in1[2], in1[1], in1[0]);
  and and_5 (and_5_out, in1[2], in1[1]);
  and and_6 (and_6_out, in1[2], in1[0]);
  and and_7 (and_7_out, in1[1], in1[0]);
  not not_6 (not_6_out, numone1_1);
  not not_7 (not_7_out, numone1_0);
  or or_1 (numone1_0, and_1_out, and_2_out, and_3_out, and_4_out);
  or or_2 (numone1_1, and_5_out, and_6_out, and_7_out);
  and and_8 (and_8_out, numone0_0, not_7_out);
  and and_9 (and_9_out, not_4_out, numone1_0);
  and and_10 (and_10_out, not_2_out, numone0_0, not_6_out, numone1_0);
  and and_11 (and_11_out, numone0_1, numone0_0, numone1_1, numone1_0);
  and and_12 (and_12_out, numone0_1, not_6_out, not_7_out);
  and and_13 (and_13_out, not_2_out, numone1_1, not_7_out);
  and and_14 (and_14_out, numone0_1, not_4_out, not_6_out);
  and and_15 (and_15_out, not_2_out, not_4_out, numone1_1);
  and and_16 (and_16_out, numone0_0, numone1_1, numone1_0);
  and and_17 (and_17_out, numone0_1, numone0_0, numone1_0);
  and and_18 (and_18_out, numone0_1, numone1_1);
  or or_3 (add[0], and_8_out, and_9_out);
  or or_4 (add[1], and_10_out, and_11_out, and_12_out, and_13_out, and_14_out, and_15_out);
  or or_5 (add[2], and_16_out, and_17_out, and_18_out);
  not not_8 (not_8_out, in0[2]);
  not not_9 (not_9_out, in0[1]);
  not not_10 (not_10_out, numone0_1);
  not not_11 (not_11_out, in0[0]);
  and and_19 (and_19_out, not_8_out, not_9_out, in0[0]);
  and and_20 (and_20_out, not_8_out, in0[1], not_11_out);
  and and_21 (and_21_out, in0[2], not_9_out, not_11_out);
  and and_22 (and_22_out, in0[2], in0[1], in0[0]);
  and and_23 (and_23_out, in0[2], in0[1]);
  and and_24 (and_24_out, in0[2], in0[0]);
  and and_25 (and_25_out, in0[1], in0[0]);
  not not_12 (not_12_out, numone0_0);
  Multiplexer #(.Bits(3)) multiplexer_1 (.sel(addsubtract), .in_0(add), .in_1({1'b0, subtract}), .out(out));
  or or_6 (numone0_0, and_19_out, and_20_out, and_21_out, and_22_out);
  or or_7 (numone0_1, and_23_out, and_24_out, and_25_out);
  not not_13 (not_13_out, numone1_1);
  not not_14 (not_14_out, numone1_0);
  and and_26 (and_26_out, not_12_out, numone1_0);
  and and_27 (and_27_out, numone0_0, not_14_out);
  and and_28 (and_28_out, numone0_1, not_13_out, not_14_out);
  and and_29 (and_29_out, numone0_1, numone0_0, not_13_out);
  or or_8 (subtract[0], and_26_out, and_27_out);
  or or_9 (subtract[1], and_28_out, and_29_out);
endmodule

/* Test case:
in0 in1 addsubtract Output 
 0b000 0b000 0 0b000
 0b000 0b001 0 0b001
 0b000 0b010 0 0b001
 0b000 0b011 0 0b010
 0b000 0b100 0 0b001
 0b000 0b101 0 0b010
 0b000 0b110 0 0b010
 0b000 0b111 0 0b011
 0b001 0b000 0 0b001
 0b001 0b001 0 0b010
 0b001 0b010 0 0b010
 0b001 0b011 0 0b011
 0b001 0b100 0 0b010
 0b001 0b101 0 0b011
 0b001 0b110 0 0b011
 0b001 0b111 0 0b100
 0b010 0b000 0 0b001
 0b010 0b001 0 0b010
 0b010 0b010 0 0b010
 0b010 0b011 0 0b011
 0b010 0b100 0 0b010
 0b010 0b101 0 0b011
 0b010 0b110 0 0b011
 0b010 0b111 0 0b100
 0b011 0b000 0 0b010
 0b011 0b001 0 0b011
 0b011 0b010 0 0b011
 0b011 0b011 0 0b100
 0b011 0b100 0 0b011
 0b011 0b101 0 0b100
 0b011 0b110 0 0b100
 0b011 0b111 0 0b101
 0b100 0b000 0 0b001
 0b100 0b001 0 0b010
 0b100 0b010 0 0b010
 0b100 0b011 0 0b011
 0b100 0b100 0 0b010
 0b100 0b101 0 0b011
 0b100 0b110 0 0b011
 0b100 0b111 0 0b100
 0b101 0b000 0 0b010
 0b101 0b001 0 0b011
 0b101 0b010 0 0b011
 0b101 0b011 0 0b100
 0b101 0b100 0 0b011
 0b101 0b101 0 0b100
 0b101 0b110 0 0b100
 0b101 0b111 0 0b101
 0b110 0b000 0 0b010
 0b110 0b001 0 0b011
 0b110 0b010 0 0b011
 0b110 0b011 0 0b100
 0b110 0b100 0 0b011
 0b110 0b101 0 0b100
 0b110 0b110 0 0b100
 0b110 0b111 0 0b101
 0b111 0b000 0 0b011
 0b111 0b001 0 0b100
 0b111 0b010 0 0b100
 0b111 0b011 0 0b101
 0b111 0b100 0 0b100
 0b111 0b101 0 0b101
 0b111 0b110 0 0b101
 0b111 0b111 0 0b110

 0b111 0b000 1 0b011
 0b111 0b001 1 0b010
 0b111 0b010 1 0b010
 0b111 0b011 1 0b001
 0b111 0b100 1 0b010
 0b111 0b101 1 0b001
 0b111 0b110 1 0b001
 0b111 0b111 1 0b000

 0b110 0b000 1 0b010
 0b110 0b001 1 0b001
 0b110 0b010 1 0b001
 0b110 0b011 1 0b000
 0b110 0b100 1 0b001
 0b110 0b101 1 0b000
 0b110 0b110 1 0b000

 0b101 0b000 1 0b010
 0b101 0b001 1 0b001
 0b101 0b010 1 0b001
 0b101 0b011 1 0b000
 0b101 0b100 1 0b001
 0b101 0b101 1 0b000
 0b101 0b110 1 0b000

 0b011 0b000 1 0b010
 0b011 0b001 1 0b001
 0b011 0b010 1 0b001
 0b011 0b011 1 0b000
 0b011 0b100 1 0b001
 0b011 0b101 1 0b000
 0b011 0b110 1 0b000

 0b100 0b000 1 0b001
 0b100 0b001 1 0b000
 0b100 0b010 1 0b000
 0b100 0b100 1 0b000

 0b010 0b000 1 0b001
 0b010 0b001 1 0b000
 0b010 0b010 1 0b000
 0b010 0b100 1 0b000

 0b001 0b000 1 0b001
 0b001 0b001 1 0b000
 0b001 0b010 1 0b000
 0b001 0b100 1 0b000

 0b000 0b000 1 0b000
*/
